// Logisim project 4-bit Full Adder & Subtractor.circ as structural Verilog: 5 circuits, main circuit 1-bit Half Adder
// HA
module _1_bit_Half_Adder (
  input  in_1,
  input  in_2,
  output out_3,
  output out_4
);

  xor xor_1 (out_3, in_1, in_2);
  and and_1 (out_4, in_1, in_2);
endmodule

module _1_bit_Full_Adder (
  input  An,
  input  Bn,
  input  C_in_n,
  output out_4,
  output out_5
);

  wire n1_bit_half_adder_1_out_3, n1_bit_half_adder_1_out_4, n1_bit_half_adder_2_out_4;

  _1_bit_Half_Adder u_1_bit_half_adder_1 (
    .in_1(An), .in_2(Bn), .out_3(n1_bit_half_adder_1_out_3), .out_4(n1_bit_half_adder_1_out_4));
  _1_bit_Half_Adder u_1_bit_half_adder_2 (
    .in_1(n1_bit_half_adder_1_out_3), .in_2(C_in_n), .out_3(out_4), .out_4(n1_bit_half_adder_2_out_4));
  or or_1 (out_5, n1_bit_half_adder_2_out_4, n1_bit_half_adder_1_out_4);
endmodule

module _2_s_Complement (
  input  A3,
  input  A2,
  input  A1,
  input  A0,
  output B3,
  output B2,
  output B1,
  output B0
);

  wire or_1_out, or_2_out, or_3_out;

  or or_1 (or_1_out, A2, A1);
  or or_2 (or_2_out, A1, A0);
  or or_3 (or_3_out, or_1_out, A0);
  xor xor_1 (B3, A3, or_3_out);
  xor xor_2 (B2, A2, or_2_out);
  xor xor_3 (B1, A1, A0);

  assign B0 = A0;
endmodule

module Adder___Subtractor (
  input  Control,
  input  A3,
  input  A2,
  input  A1,
  input  A0,
  input  B3,
  input  B2,
  input  B1,
  input  B0,
  input  Enable,
  output Sign,
  output S4,
  output S3___D3,
  output S2___D2,
  output S1___D1,
  output S0___D0
);

  wire and_1_out, and_2_out, and_3_out, and_4_out, and_5_out, and_6_out, and_7_out, and_8_out,
       n1_bit_full_adder_1_out_4, n1_bit_full_adder_1_out_5, n1_bit_full_adder_2_out_4,
       n1_bit_full_adder_2_out_5, n1_bit_full_adder_3_out_4, n1_bit_full_adder_3_out_5,
       n1_bit_full_adder_4_out_4, n1_bit_full_adder_4_out_5, n2_s_complement_1_b0, n2_s_complement_1_b1,
       n2_s_complement_1_b2, n2_s_complement_1_b3, not_1_out, not_2_out, xor_1_out, xor_2_out, xor_3_out,
       xor_4_out;

  and and_1 (and_1_out, A3, Enable);
  and and_2 (and_2_out, A2, Enable);
  and and_3 (and_3_out, A1, Enable);
  and and_4 (and_4_out, A0, Enable);
  and and_5 (and_5_out, B3, Enable);
  and and_6 (and_6_out, B2, Enable);
  and and_7 (and_7_out, B1, Enable);
  and and_8 (and_8_out, B0, Enable);
  xor xor_1 (xor_1_out, and_5_out, Control);
  xor xor_2 (xor_2_out, and_6_out, Control);
  xor xor_3 (xor_3_out, and_7_out, Control);
  xor xor_4 (xor_4_out, and_8_out, Control);
  _1_bit_Full_Adder u_1_bit_full_adder_1 (
    .An(and_1_out), .Bn(xor_1_out), .C_in_n(n1_bit_full_adder_2_out_5), .out_4(n1_bit_full_adder_1_out_4),
    .out_5(n1_bit_full_adder_1_out_5));
  _1_bit_Full_Adder u_1_bit_full_adder_2 (
    .An(and_2_out), .Bn(xor_2_out), .C_in_n(n1_bit_full_adder_3_out_5), .out_4(n1_bit_full_adder_2_out_4),
    .out_5(n1_bit_full_adder_2_out_5));
  _1_bit_Full_Adder u_1_bit_full_adder_3 (
    .An(and_3_out), .Bn(xor_3_out), .C_in_n(n1_bit_full_adder_4_out_5), .out_4(n1_bit_full_adder_3_out_4),
    .out_5(n1_bit_full_adder_3_out_5));
  _1_bit_Full_Adder u_1_bit_full_adder_4 (
    .An(and_4_out), .Bn(xor_4_out), .C_in_n(Control), .out_4(n1_bit_full_adder_4_out_4),
    .out_5(n1_bit_full_adder_4_out_5));
  not not_1 (not_1_out, n1_bit_full_adder_1_out_5);
  not not_2 (not_2_out, Control);
  and Subtractor_Case (Sign, not_1_out, Control);
  and Adder_Case (S4, n1_bit_full_adder_1_out_5, not_2_out);
  _2_s_Complement u_2_s_complement_1 (
    .A3(n1_bit_full_adder_1_out_4), .A2(n1_bit_full_adder_2_out_4), .A1(n1_bit_full_adder_3_out_4),
    .A0(n1_bit_full_adder_4_out_4), .B3(n2_s_complement_1_b3), .B2(n2_s_complement_1_b2),
    .B1(n2_s_complement_1_b1), .B0(n2_s_complement_1_b0));
  _2_bit_MUX u_2_bit_mux_1 (
    .in_1(n1_bit_full_adder_1_out_4), .in_2(Sign), .in_3(n2_s_complement_1_b3), .out_4(S3___D3));
  _2_bit_MUX u_2_bit_mux_2 (
    .in_1(n1_bit_full_adder_2_out_4), .in_2(Sign), .in_3(n2_s_complement_1_b2), .out_4(S2___D2));
  _2_bit_MUX u_2_bit_mux_3 (
    .in_1(n1_bit_full_adder_3_out_4), .in_2(Sign), .in_3(n2_s_complement_1_b1), .out_4(S1___D1));
  _2_bit_MUX u_2_bit_mux_4 (
    .in_1(n1_bit_full_adder_4_out_4), .in_2(Sign), .in_3(n2_s_complement_1_b0), .out_4(S0___D0));

  // Notes on the sheet:
  //   MSB
  //   LSB
  //   MSB
  //   LSB
endmodule

module _2_bit_MUX (
  input  in_1,
  input  in_2,
  input  in_3,
  output out_4
);

  wire and_1_out, and_2_out, not_1_out;

  not not_1 (not_1_out, in_2);
  and and_1 (and_1_out, in_1, not_1_out);
  and and_2 (and_2_out, in_2, in_3);
  or or_1 (out_4, and_1_out, and_2_out);
endmodule
