// Logisim project 4-bit Full Adder & Subtractor.circ as structural Verilog: 3 circuits, main circuit 1-bit Half Adder
// HA
module _1_bit_Half_Adder (
  input  in_1,
  input  in_2,
  output out_3,
  output out_4
);

  xor xor_1 (out_3, in_1, in_2);
  and and_1 (out_4, in_1, in_2);
endmodule

module _1_bit_Full_Adder (
  input  in_1,
  input  in_2,
  input  in_3,
  output out_4,
  output out_5
);

  wire n1_bit_half_adder_1_out_3, n1_bit_half_adder_1_out_4, n1_bit_half_adder_2_out_4;

  _1_bit_Half_Adder u_1_bit_half_adder_1 (
    .in_1(in_1), .in_2(in_2), .out_3(n1_bit_half_adder_1_out_3), .out_4(n1_bit_half_adder_1_out_4));
  _1_bit_Half_Adder u_1_bit_half_adder_2 (
    .in_1(n1_bit_half_adder_1_out_3), .in_2(in_3), .out_3(out_4), .out_4(n1_bit_half_adder_2_out_4));
  or or_1 (out_5, n1_bit_half_adder_2_out_4, n1_bit_half_adder_1_out_4);
endmodule

module _4_bit_Full_Adder__Subtractor (
  input  control,
  input  A0,
  input  A1,
  input  A2,
  input  A3,
  input  B0,
  input  B1,
  input  B2,
  input  B3,
  output out_10,
  output out_11,
  output out_12,
  output out_13,
  output out_14
);

  wire n1_bit_full_adder_1_out_5, n1_bit_full_adder_2_out_5, n1_bit_full_adder_3_out_5, xor_1_out, xor_2_out,
       xor_3_out, xor_4_out;

  xor xor_1 (xor_1_out, B0, control);
  xor xor_2 (xor_2_out, B1, control);
  xor xor_3 (xor_3_out, B2, control);
  xor xor_4 (xor_4_out, B3, control);
  _1_bit_Full_Adder u_1_bit_full_adder_1 (
    .in_1(A0), .in_2(xor_1_out), .in_3(control), .out_4(out_10), .out_5(n1_bit_full_adder_1_out_5));
  _1_bit_Full_Adder u_1_bit_full_adder_2 (
    .in_1(A1), .in_2(xor_2_out), .in_3(n1_bit_full_adder_1_out_5), .out_4(out_11),
    .out_5(n1_bit_full_adder_2_out_5));
  _1_bit_Full_Adder u_1_bit_full_adder_3 (
    .in_1(A2), .in_2(xor_3_out), .in_3(n1_bit_full_adder_2_out_5), .out_4(out_12),
    .out_5(n1_bit_full_adder_3_out_5));
  _1_bit_Full_Adder u_1_bit_full_adder_4 (
    .in_1(A3), .in_2(xor_4_out), .in_3(n1_bit_full_adder_3_out_5), .out_4(out_13), .out_5(out_14));
endmodule
