// Logisim project 8-bit MUX.circ as structural Verilog: 2 circuits, main circuit main
module main (
  input  in_1,
  input  B,
  input  Selector,
  output out_4
);

  wire and_1_out, and_2_out, not_1_out;

  not not_1 (not_1_out, Selector);
  and and_1 (and_1_out, in_1, not_1_out);
  and and_2 (and_2_out, B, Selector);
  or or_1 (out_4, and_1_out, and_2_out);

  // Notes on the sheet:
  //   A
endmodule

module _8_bit_MUX (
  input  A0,
  input  A1,
  input  A2,
  input  A3,
  input  B0,
  input  B1,
  input  B2,
  input  B3,
  input  selector,
  output out_10,
  output out_11,
  output out_12,
  output out_13
);

  main main_1 (.in_1(A0), .B(B0), .Selector(selector), .out_4(out_10));
  main main_2 (.in_1(A1), .B(B1), .Selector(selector), .out_4(out_11));
  main main_3 (.in_1(A2), .B(B2), .Selector(selector), .out_4(out_12));
  main main_4 (.in_1(A3), .B(B3), .Selector(selector), .out_4(out_13));

  // Notes on the sheet:
  //   2x1 MUX
  //   2x1 MUX
  //   2x1 MUX
  //   2x1 MUX
endmodule
