// Logisim project BCDto7.circ as structural Verilog: 3 circuits, main circuit main
module main (
  input  B,
  input  C,
  input  D,
  input  A,
  output a_2,
  output b_2,
  output c_2,
  output d_2,
  output e,
  output f,
  output g
);

  wire B_prime_C_out, B_prime_D_prime_out, BC_prime_D_out, BC_prime_out, BD_out, BD_prime_out,
       C_prime_D_prime_out, CD_out, CD_prime_out, not_1_out, not_2_out, not_3_out, not_4_out;

  not not_1 (not_1_out, A);
  not not_2 (not_2_out, B);
  not not_3 (not_3_out, C);
  not not_4 (not_4_out, D);
  and BD (BD_out, B, D);
  and B_prime_D_prime (B_prime_D_prime_out, not_2_out, not_4_out);
  and CD (CD_out, C, D);
  and C_prime_D_prime (C_prime_D_prime_out, not_3_out, not_4_out);
  and CD_prime (CD_prime_out, C, not_4_out);
  and B_prime_C (B_prime_C_out, not_2_out, C);
  and BC_prime_D (BC_prime_D_out, D, BC_prime_out);
  and BC_prime (BC_prime_out, B, not_3_out);
  and BD_prime (BD_prime_out, B, not_4_out);
  or u_a (a_2, BD_out, B_prime_D_prime_out, C, A);
  or u_b (b_2, CD_out, C_prime_D_prime_out, not_2_out);
  or u_c (c_2, D, not_3_out, B);
  or u_d (d_2, B_prime_D_prime_out, A, CD_prime_out, B_prime_C_out, BC_prime_D_out);
  or u_f (f, C_prime_D_prime_out, BC_prime_out, BD_prime_out, A);
  or u_g (g, CD_prime_out, BC_prime_out, B_prime_C_out, A);
  or u_e (e, B_prime_D_prime_out, CD_prime_out);
endmodule

module for_trying (
  input  [3:0] in_1,
  input  [3:0] in_2,
  input  [3:0] in_3
);

  wire bcdto7segmant_1_a_2, bcdto7segmant_1_b_2, bcdto7segmant_1_c_2, bcdto7segmant_1_d_2, bcdto7segmant_1_e,
       bcdto7segmant_1_f, bcdto7segmant_1_g;

  _7_Segment_Display u_7_segment_display_1 (
    .g(in_1[3]), .f(in_1[2]), .a(in_1[1]), .b(in_1[0]), .e(in_2[0]), .d(in_2[1]), .c(in_2[2]), .dp(in_2[3]));
  bcdto7segmant bcdto7segmant_1 (
    .A(in_3[3]), .a_2(bcdto7segmant_1_a_2), .b_2(bcdto7segmant_1_b_2), .c_2(bcdto7segmant_1_c_2),
    .d_2(bcdto7segmant_1_d_2), .e(bcdto7segmant_1_e), .f(bcdto7segmant_1_f), .g(bcdto7segmant_1_g),
    .B(in_3[2]), .C(in_3[1]), .D(in_3[0]));
  _7_Segment_Display u_7_segment_display_2 (
    .g(bcdto7segmant_1_g), .f(bcdto7segmant_1_f), .a(bcdto7segmant_1_a_2), .b(bcdto7segmant_1_b_2),
    .e(bcdto7segmant_1_e), .d(bcdto7segmant_1_d_2), .c(bcdto7segmant_1_c_2));  // open: dp
endmodule

module bcdto7segmant (
  input  A,
  input  B,
  input  C,
  input  D,
  output a_2,
  output b_2,
  output c_2,
  output d_2,
  output e,
  output f,
  output g
);

  wire B_prime_C_out, B_prime_D_prime_out, BC_prime_D_out, BC_prime_out, BD_out, BD_prime_out,
       C_prime_D_prime_out, CD_out, CD_prime_out, not_1_out, not_2_out, not_3_out, not_4_out;

  not not_1 (not_1_out, A);
  not not_2 (not_2_out, B);
  not not_3 (not_3_out, C);
  not not_4 (not_4_out, D);
  and BD (BD_out, B, D);
  and B_prime_D_prime (B_prime_D_prime_out, not_2_out, not_4_out);
  and CD (CD_out, C, D);
  and C_prime_D_prime (C_prime_D_prime_out, not_3_out, not_4_out);
  and CD_prime (CD_prime_out, C, not_4_out);
  and B_prime_C (B_prime_C_out, not_2_out, C);
  and BC_prime_D (BC_prime_D_out, D, BC_prime_out);
  and BC_prime (BC_prime_out, B, not_3_out);
  and BD_prime (BD_prime_out, B, not_4_out);
  or u_a (a_2, BD_out, B_prime_D_prime_out, C, A);
  or u_b (b_2, CD_out, C_prime_D_prime_out, not_2_out);
  or u_c (c_2, D, not_3_out, B);
  or u_d (d_2, B_prime_D_prime_out, A, CD_prime_out, B_prime_C_out, BC_prime_D_out);
  or u_e (e, B_prime_D_prime_out, CD_prime_out);
  or u_f (f, C_prime_D_prime_out, BC_prime_out, BD_prime_out, A);
  or u_g (g, CD_prime_out, BC_prime_out, B_prime_C_out, A);
endmodule
