// Logisim project Binary To BCD.circ as structural Verilog: 4 circuits, main circuit combined
module Binary_to_BCD (
  input  a,
  input  b,
  input  c,
  input  d,
  output x,
  output y,
  output z,
  output u
);

  wire and_1_out, and_2_out, and_3_out, and_4_out, and_5_out, and_6_out, and_7_out, and_8_out, and_9_out,
       and_10_out, and_11_out, and_12_out, and_13_out, and_14_out, and_15_out, and_16_out, not_1_out,
       not_2_out, not_3_out, not_4_out, not_5_out, not_6_out, not_7_out, not_8_out, not_9_out, not_10_out,
       not_11_out, or_1_out, or_4_out, or_5_out;

  and and_1 (and_1_out, b, d);
  and and_2 (and_2_out, b, c);
  and and_3 (and_3_out, b, not_1_out);
  not not_1 (not_1_out, c);
  not not_2 (not_2_out, d);
  not not_3 (not_3_out, a);
  and and_4 (and_4_out, not_3_out, not_4_out);
  not not_4 (not_4_out, b);
  not not_5 (not_5_out, c);
  not not_6 (not_6_out, a);
  and and_5 (and_5_out, not_6_out, not_7_out);
  not not_7 (not_7_out, b);
  and and_6 (and_6_out, b, c);
  not not_8 (not_8_out, d);
  not not_9 (not_9_out, c);
  or or_1 (or_1_out, and_1_out, and_2_out);
  or or_2 (x, or_1_out, a);
  and and_7 (and_7_out, and_3_out, not_2_out);
  and and_8 (and_8_out, a, d);
  and and_9 (and_9_out, and_4_out, c);
  and and_10 (and_10_out, c, d);
  and and_11 (and_11_out, a, not_5_out);
  not not_10 (not_10_out, d);
  and and_12 (and_12_out, and_5_out, d);
  and and_13 (and_13_out, and_6_out, not_8_out);
  and and_14 (and_14_out, a, not_9_out);
  not not_11 (not_11_out, d);
  or or_3 (y, and_7_out, and_8_out);
  or or_4 (or_4_out, and_9_out, and_10_out);
  and and_15 (and_15_out, and_11_out, not_10_out);
  or or_5 (or_5_out, and_12_out, and_13_out);
  and and_16 (and_16_out, and_14_out, not_11_out);
  or or_6 (z, or_4_out, and_15_out);
  or or_7 (u, or_5_out, and_16_out);
endmodule

// p8
module main (
  input  B7,
  input  B6,
  input  B5,
  input  B4,
  input  B3,
  input  B2,
  input  B1,
  input  B0,
  output p9,
  output p8,
  output p7,
  output p6,
  output p5,
  output p4,
  output p3,
  output p2,
  output p1,
  output p0
);

  wire C1_u, C1_x, C1_y, C1_z, C2_u, C2_x, C2_y, C2_z, C3_u, C3_x, C3_y, C3_z, C4_u, C4_x, C4_y, C4_z, C6_u,
       C6_y, C6_z;

  Binary_to_BCD C1 (.a(1'b0), .b(B7), .c(B6), .d(B5), .x(C1_x), .y(C1_y), .z(C1_z), .u(C1_u));
  Binary_to_BCD C2 (.a(C1_y), .b(C1_z), .c(C1_u), .d(B4), .x(C2_x), .y(C2_y), .z(C2_z), .u(C2_u));
  Binary_to_BCD C3 (.a(C2_y), .b(C2_z), .c(C2_u), .d(B3), .x(C3_x), .y(C3_y), .z(C3_z), .u(C3_u));
  Binary_to_BCD C6 (.a(1'b0), .b(C1_x), .c(C2_x), .d(C3_x), .x(p9), .y(C6_y), .z(C6_z), .u(C6_u));
  Binary_to_BCD C4 (.a(C3_y), .b(C3_z), .c(C3_u), .d(B2), .x(C4_x), .y(C4_y), .z(C4_z), .u(C4_u));
  Binary_to_BCD C7 (.a(C6_y), .b(C6_z), .c(C6_u), .d(C4_x), .x(p8), .y(p7), .z(p6), .u(p5));
  Binary_to_BCD C5 (.a(C4_y), .b(C4_z), .c(C4_u), .d(B1), .x(p4), .y(p3), .z(p2), .u(p1));

  assign p0 = B0;
endmodule

module combined (
  input  [7:0] in_1
);

  wire bcd_to_7segment_1_a_2, bcd_to_7segment_1_b_2, bcd_to_7segment_1_c_2, bcd_to_7segment_1_d_2,
       bcd_to_7segment_1_e, bcd_to_7segment_1_f, bcd_to_7segment_1_g, bcd_to_7segment_2_a_2,
       bcd_to_7segment_2_b_2, bcd_to_7segment_2_c_2, bcd_to_7segment_2_d_2, bcd_to_7segment_2_e,
       bcd_to_7segment_2_f, bcd_to_7segment_2_g, bcd_to_7segment_3_a_2, bcd_to_7segment_3_b_2,
       bcd_to_7segment_3_c_2, bcd_to_7segment_3_d_2, bcd_to_7segment_3_e, bcd_to_7segment_3_f,
       bcd_to_7segment_3_g, main_1_p0, main_1_p1, main_1_p2, main_1_p3, main_1_p4, main_1_p5, main_1_p6,
       main_1_p7, main_1_p8, main_1_p9;

  main main_1 (
    .B7(in_1[7]), .B6(in_1[6]), .B5(in_1[5]), .B4(in_1[4]), .B3(in_1[3]), .B2(in_1[2]), .B1(in_1[1]),
    .B0(in_1[0]), .p9(main_1_p9), .p8(main_1_p8), .p7(main_1_p7), .p6(main_1_p6), .p5(main_1_p5),
    .p4(main_1_p4), .p3(main_1_p3), .p2(main_1_p2), .p1(main_1_p1), .p0(main_1_p0));
  bcd_to_7segment bcd_to_7segment_1 (
    .A(1'b0), .B(1'b0), .C(main_1_p9), .D(main_1_p8), .a_2(bcd_to_7segment_1_a_2),
    .b_2(bcd_to_7segment_1_b_2), .c_2(bcd_to_7segment_1_c_2), .d_2(bcd_to_7segment_1_d_2),
    .e(bcd_to_7segment_1_e), .f(bcd_to_7segment_1_f), .g(bcd_to_7segment_1_g));
  _7_Segment_Display u_7_segment_display_1 (
    .g(bcd_to_7segment_1_g), .f(bcd_to_7segment_1_f), .a(bcd_to_7segment_1_a_2), .b(bcd_to_7segment_1_b_2),
    .e(bcd_to_7segment_1_e), .d(bcd_to_7segment_1_d_2), .c(bcd_to_7segment_1_c_2));  // open: dp
  bcd_to_7segment bcd_to_7segment_2 (
    .A(main_1_p3), .B(main_1_p2), .C(main_1_p1), .D(main_1_p0), .a_2(bcd_to_7segment_2_a_2),
    .b_2(bcd_to_7segment_2_b_2), .c_2(bcd_to_7segment_2_c_2), .d_2(bcd_to_7segment_2_d_2),
    .e(bcd_to_7segment_2_e), .f(bcd_to_7segment_2_f), .g(bcd_to_7segment_2_g));
  _7_Segment_Display u_7_segment_display_2 (
    .g(bcd_to_7segment_2_g), .f(bcd_to_7segment_2_f), .a(bcd_to_7segment_2_a_2), .b(bcd_to_7segment_2_b_2),
    .e(bcd_to_7segment_2_e), .d(bcd_to_7segment_2_d_2), .c(bcd_to_7segment_2_c_2));  // open: dp
  bcd_to_7segment bcd_to_7segment_3 (
    .A(main_1_p7), .B(main_1_p6), .C(main_1_p5), .D(main_1_p4), .a_2(bcd_to_7segment_3_a_2),
    .b_2(bcd_to_7segment_3_b_2), .c_2(bcd_to_7segment_3_c_2), .d_2(bcd_to_7segment_3_d_2),
    .e(bcd_to_7segment_3_e), .f(bcd_to_7segment_3_f), .g(bcd_to_7segment_3_g));
  _7_Segment_Display u_7_segment_display_3 (
    .g(bcd_to_7segment_3_g), .f(bcd_to_7segment_3_f), .a(bcd_to_7segment_3_a_2), .b(bcd_to_7segment_3_b_2),
    .e(bcd_to_7segment_3_e), .d(bcd_to_7segment_3_d_2), .c(bcd_to_7segment_3_c_2));  // open: dp
endmodule

module bcd_to_7segment (
  input  A,
  input  B,
  input  C,
  input  D,
  output a_2,
  output b_2,
  output c_2,
  output d_2,
  output e,
  output f,
  output g
);

  wire B_prime_C_out, B_prime_D_prime_out, BC_prime_D_out, BC_prime_out, BD_out, BD_prime_out,
       C_prime_D_prime_out, CD_out, CD_prime_out, not_1_out, not_2_out, not_3_out, not_4_out;

  not not_1 (not_1_out, A);
  not not_2 (not_2_out, B);
  not not_3 (not_3_out, C);
  not not_4 (not_4_out, D);
  and BD (BD_out, B, D);
  and B_prime_D_prime (B_prime_D_prime_out, not_2_out, not_4_out);
  and CD (CD_out, C, D);
  and C_prime_D_prime (C_prime_D_prime_out, not_3_out, not_4_out);
  and CD_prime (CD_prime_out, C, not_4_out);
  and B_prime_C (B_prime_C_out, not_2_out, C);
  and BC_prime_D (BC_prime_D_out, D, BC_prime_out);
  and BC_prime (BC_prime_out, B, not_3_out);
  and BD_prime (BD_prime_out, B, not_4_out);
  or u_a (a_2, BD_out, B_prime_D_prime_out, C, A);
  or u_b (b_2, CD_out, C_prime_D_prime_out, not_2_out);
  or u_c (c_2, D, not_3_out, B);
  or u_d (d_2, B_prime_D_prime_out, A, CD_prime_out, B_prime_C_out, BC_prime_D_out);
  or u_e (e, B_prime_D_prime_out, CD_prime_out);
  or u_f (f, C_prime_D_prime_out, BC_prime_out, BD_prime_out, A);
  or u_g (g, CD_prime_out, BC_prime_out, B_prime_C_out, A);
endmodule
