// Logisim project FINAL CIRC.circ as structural Verilog: 15 circuits, main circuit main
module main (
  input  signal_1,
  input  signal_2,
  input  A_sign,
  input  A3,
  input  in_5,
  input  in_6,
  input  A0,
  input  B_sign,
  input  B3,
  input  in_10,
  input  in_11,
  input  B0,
  output div_by_0,
  output Zero
);

  wire alu_1_p0, alu_1_p1, alu_1_p2, alu_1_p3, alu_1_p4, alu_1_p5, alu_1_p6, alu_1_p7, alu_1_p8, alu_1_p9,
       alu_1_sign, bcd_to_7segment_1_a_2, bcd_to_7segment_1_b_2, bcd_to_7segment_1_c_2,
       bcd_to_7segment_1_d_2, bcd_to_7segment_1_e, bcd_to_7segment_1_f, bcd_to_7segment_1_g,
       bcd_to_7segment_2_a_2, bcd_to_7segment_2_b_2, bcd_to_7segment_2_c_2, bcd_to_7segment_2_d_2,
       bcd_to_7segment_2_e, bcd_to_7segment_2_f, bcd_to_7segment_2_g, bcd_to_7segment_3_a_2,
       bcd_to_7segment_3_b_2, bcd_to_7segment_3_c_2, bcd_to_7segment_3_d_2, bcd_to_7segment_3_e,
       bcd_to_7segment_3_f, bcd_to_7segment_3_g;

  ALU alu_1 (
    .signal_1(signal_1), .signal_2(signal_2), .A_sign(A_sign), .A3(A3), .in_5(in_5), .in_6(in_6), .A0(A0),
    .B_sign(B_sign), .B3(B3), .in_10(in_10), .in_11(in_11), .B0(B0), .P9(alu_1_p9), .P8(alu_1_p8),
    .P7(alu_1_p7), .P6(alu_1_p6), .P5(alu_1_p5), .P4(alu_1_p4), .P3(alu_1_p3), .P2(alu_1_p2), .P1(alu_1_p1),
    .P0(alu_1_p0), .div_by_0(div_by_0), .sign(alu_1_sign), .Zero(Zero));
  _7_Segment_Display u_7_segment_display_1 (.g(alu_1_sign));  // open: f, a, b, e, d, c, dp
  bcd_to_7segment bcd_to_7segment_1 (
    .A(1'b0), .B(1'b0), .C(alu_1_p9), .D(alu_1_p8), .a_2(bcd_to_7segment_1_a_2), .b_2(bcd_to_7segment_1_b_2),
    .c_2(bcd_to_7segment_1_c_2), .d_2(bcd_to_7segment_1_d_2), .e(bcd_to_7segment_1_e),
    .f(bcd_to_7segment_1_f), .g(bcd_to_7segment_1_g));
  _7_Segment_Display u_7_segment_display_2 (
    .g(bcd_to_7segment_1_g), .f(bcd_to_7segment_1_f), .a(bcd_to_7segment_1_a_2), .b(bcd_to_7segment_1_b_2),
    .e(bcd_to_7segment_1_e), .d(bcd_to_7segment_1_d_2), .c(bcd_to_7segment_1_c_2));  // open: dp
  bcd_to_7segment bcd_to_7segment_2 (
    .A(alu_1_p3), .B(alu_1_p2), .C(alu_1_p1), .D(alu_1_p0), .a_2(bcd_to_7segment_2_a_2),
    .b_2(bcd_to_7segment_2_b_2), .c_2(bcd_to_7segment_2_c_2), .d_2(bcd_to_7segment_2_d_2),
    .e(bcd_to_7segment_2_e), .f(bcd_to_7segment_2_f), .g(bcd_to_7segment_2_g));
  bcd_to_7segment bcd_to_7segment_3 (
    .A(alu_1_p7), .B(alu_1_p6), .C(alu_1_p5), .D(alu_1_p4), .a_2(bcd_to_7segment_3_a_2),
    .b_2(bcd_to_7segment_3_b_2), .c_2(bcd_to_7segment_3_c_2), .d_2(bcd_to_7segment_3_d_2),
    .e(bcd_to_7segment_3_e), .f(bcd_to_7segment_3_f), .g(bcd_to_7segment_3_g));
  _7_Segment_Display u_7_segment_display_3 (
    .g(bcd_to_7segment_2_g), .f(bcd_to_7segment_2_f), .a(bcd_to_7segment_2_a_2), .b(bcd_to_7segment_2_b_2),
    .e(bcd_to_7segment_2_e), .d(bcd_to_7segment_2_d_2), .c(bcd_to_7segment_2_c_2));  // open: dp
  _7_Segment_Display u_7_segment_display_4 (
    .g(bcd_to_7segment_3_g), .f(bcd_to_7segment_3_f), .a(bcd_to_7segment_3_a_2), .b(bcd_to_7segment_3_b_2),
    .e(bcd_to_7segment_3_e), .d(bcd_to_7segment_3_d_2), .c(bcd_to_7segment_3_c_2));  // open: dp

  // Notes on the sheet:
  //   Mod of operation
  //   SIgn
  //   MSB
  //   LSB
endmodule

module out_2 (
  input  signal_1,
  input  signal_2,
  input  A_sign,
  input  B_sign,
  output out_2
);

  wire AB_out, and_1_out, and_2_out, not_1_out, not_2_out, not_3_out, xor_1_out;

  not not_1 (not_1_out, signal_1);
  not not_2 (not_2_out, signal_2);
  xor xor_1 (xor_1_out, A_sign, B_sign);
  and AB (AB_out, signal_1, signal_2);
  not not_3 (not_3_out, xor_1_out);
  and and_1 (and_1_out, not_1_out, not_2_out, xor_1_out);
  and and_2 (and_2_out, not_3_out, signal_2);
  or or_1 (out_2, AB_out, and_1_out, and_2_out);
endmodule

module sign (
  input  signal_1,
  input  signal_2,
  input  A_sign,
  input  B_sign,
  output sign
);

  wire and_1_out, and_2_out, and_3_out, and_4_out, not_1_out, not_2_out, not_3_out, not_4_out;

  not not_1 (not_1_out, signal_1);
  not not_2 (not_2_out, signal_2);
  not not_3 (not_3_out, B_sign);
  not not_4 (not_4_out, A_sign);
  and and_1 (and_1_out, signal_1, not_4_out, B_sign);
  and and_2 (and_2_out, not_1_out, not_2_out, A_sign, B_sign);
  and and_3 (and_3_out, signal_2, A_sign, not_3_out);
  or or_1 (sign, and_2_out, and_3_out, and_1_out, and_4_out);
  and and_4 (and_4_out, signal_1, A_sign, not_3_out);
endmodule

module exchange (
  input  signal_1,
  input  signal_2,
  input  A_sign,
  input  B_sign,
  output Exchange
);

  wire and_1_out, and_2_out, and_3_out, and_4_out, and_5_out, and_6_out, not_1_out, not_2_out, not_3_out;

  not not_1 (not_1_out, signal_1);
  not not_2 (not_2_out, signal_2);
  not not_3 (not_3_out, B_sign);
  and and_1 (and_1_out, not_1_out, not_2_out);
  and and_2 (and_2_out, A_sign, not_3_out);
  and and_3 (and_3_out, not_1_out, signal_2);
  and and_4 (and_4_out, A_sign, B_sign);
  and and_5 (and_5_out, and_1_out, and_2_out);
  and and_6 (and_6_out, and_3_out, and_4_out);
  or or_1 (Exchange, and_5_out, and_6_out);
endmodule

module sign_manager (
  input  signal_1,
  input  signal_2,
  input  A_sign,
  input  B_sign,
  output out_1,
  output out_2,
  output sign,
  output exchange
);

  out_2 out_2_1 (.signal_1(signal_1), .signal_2(signal_2), .A_sign(A_sign), .B_sign(B_sign), .out_2(out_2));
  sign sign_1 (.signal_1(signal_1), .signal_2(signal_2), .A_sign(A_sign), .B_sign(B_sign), .sign(sign));
  exchange exchange_1 (.signal_1(signal_1), .signal_2(signal_2), .Exchange(exchange), .A_sign(A_sign), .B_sign(B_sign));

  assign out_1 = signal_1;
endmodule

module op_selector (
  input  out_1,
  input  out_2,
  output Add,
  output sub,
  output multi,
  output div
);

  wire not_1_out, not_2_out;

  not not_1 (not_1_out, out_1);
  not not_2 (not_2_out, out_2);
  and and_1 (Add, not_1_out, not_2_out);
  and and_2 (sub, not_1_out, out_2);
  and and_3 (multi, out_1, not_2_out);
  and and_4 (div, out_1, out_2);
endmodule

module multi (
  input  A3,
  input  A2,
  input  A1,
  input  A0,
  input  B3,
  input  B2,
  input  B1,
  input  B0,
  input  Enable,
  output M0,
  output m1,
  output M2,
  output M3,
  output M4,
  output M5,
  output M6,
  output M7
);

  wire and_1_out, and_2_out, and_3_out, and_4_out, and_5_out, and_6_out, and_7_out, and_8_out, and_9_out,
       and_10_out, and_11_out, and_12_out, and_13_out, and_14_out, and_15_out, and_16_out,
       unsigned_4_bit_full_adder_1_s0, unsigned_4_bit_full_adder_1_s1, unsigned_4_bit_full_adder_1_s2,
       unsigned_4_bit_full_adder_1_s3, unsigned_4_bit_full_adder_1_s4, unsigned_4_bit_full_adder_2_s0,
       unsigned_4_bit_full_adder_2_s1, unsigned_4_bit_full_adder_2_s2, unsigned_4_bit_full_adder_2_s3,
       unsigned_4_bit_full_adder_2_s4, unsigned_4_bit_full_adder_3_s0, unsigned_4_bit_full_adder_3_s1,
       unsigned_4_bit_full_adder_3_s2, unsigned_4_bit_full_adder_3_s3, unsigned_4_bit_full_adder_3_s4;

  and and_1 (and_1_out, B3, A1);
  and and_2 (and_2_out, B2, A1);
  and and_3 (and_3_out, B1, A1);
  and and_4 (and_4_out, B0, A1);
  and and_5 (and_5_out, B0, A2);
  and and_6 (and_6_out, B1, A2);
  and and_7 (and_7_out, B3, A0);
  and and_8 (and_8_out, B2, A2);
  and and_9 (and_9_out, B3, A2);
  and and_10 (and_10_out, B2, A0);
  and and_11 (and_11_out, B1, A0);
  and and_12 (and_12_out, B3, A3);
  Unsigned_4_bit_Full_Adder unsigned_4_bit_full_adder_1 (
    .A3(1'b0), .A2(and_7_out), .A1(and_10_out), .A0(and_11_out), .B3(and_1_out), .B2(and_2_out),
    .B1(and_3_out), .B0(and_4_out), .C_in_1___0(1'b0), .S4(unsigned_4_bit_full_adder_1_s4),
    .S3(unsigned_4_bit_full_adder_1_s3), .S2(unsigned_4_bit_full_adder_1_s2),
    .S1(unsigned_4_bit_full_adder_1_s1), .S0(unsigned_4_bit_full_adder_1_s0));
  and and_13 (and_13_out, B2, A3);
  and and_14 (and_14_out, B0, A0);
  and and_15 (and_15_out, B1, A3);
  Unsigned_4_bit_Full_Adder unsigned_4_bit_full_adder_2 (
    .A3(unsigned_4_bit_full_adder_1_s4), .A2(unsigned_4_bit_full_adder_1_s3),
    .A1(unsigned_4_bit_full_adder_1_s2), .A0(unsigned_4_bit_full_adder_1_s1), .B3(and_9_out), .B2(and_8_out),
    .B1(and_6_out), .B0(and_5_out), .C_in_1___0(1'b0), .S4(unsigned_4_bit_full_adder_2_s4),
    .S3(unsigned_4_bit_full_adder_2_s3), .S2(unsigned_4_bit_full_adder_2_s2),
    .S1(unsigned_4_bit_full_adder_2_s1), .S0(unsigned_4_bit_full_adder_2_s0));
  and and_16 (and_16_out, B0, A3);
  Unsigned_4_bit_Full_Adder unsigned_4_bit_full_adder_3 (
    .A3(unsigned_4_bit_full_adder_2_s4), .A2(unsigned_4_bit_full_adder_2_s3),
    .A1(unsigned_4_bit_full_adder_2_s2), .A0(unsigned_4_bit_full_adder_2_s1), .B3(and_12_out),
    .B2(and_13_out), .B1(and_15_out), .B0(and_16_out), .C_in_1___0(1'b0),
    .S4(unsigned_4_bit_full_adder_3_s4), .S3(unsigned_4_bit_full_adder_3_s3),
    .S2(unsigned_4_bit_full_adder_3_s2), .S1(unsigned_4_bit_full_adder_3_s1),
    .S0(unsigned_4_bit_full_adder_3_s0));
  and and_17 (M2, Enable, unsigned_4_bit_full_adder_2_s0);
  and and_18 (M0, Enable, and_14_out);
  and and_19 (m1, Enable, unsigned_4_bit_full_adder_1_s0);
  and and_20 (M3, Enable, unsigned_4_bit_full_adder_3_s0);
  and and_21 (M4, Enable, unsigned_4_bit_full_adder_3_s1);
  and and_22 (M6, Enable, unsigned_4_bit_full_adder_3_s3);
  and and_23 (M7, Enable, unsigned_4_bit_full_adder_3_s4);
  and and_24 (M5, Enable, unsigned_4_bit_full_adder_3_s2);

  // Notes on the sheet:
  //   A3
  //   A0
  //   B3
  //   B0
  //   CIN
  //   A1B3
  //   A1B2
  //   A1B1
  //   A2B0
  //   A1B0
  //   A2B1
  //   A2B2
  //   A0B3
  //   A2B3
  //   A0B2
  //   A3B3
  //   A0B1
  //   A3B2
  //   A0B0
  //   A3B1
  //   A3B0
endmodule

module _8_bit_mux (
  input  A3,
  input  A2,
  input  A1,
  input  A0,
  input  B3,
  input  B2,
  input  B1,
  input  B0,
  input  selector,
  output out_3,
  output out_2,
  output out_1,
  output out_0
);

  _8_bit_MUX_main main_1 (.in_1(A0), .B(B0), .Selector(selector), .out_4(out_0));
  _8_bit_MUX_main main_2 (.in_1(A1), .B(B1), .Selector(selector), .out_4(out_1));
  _8_bit_MUX_main main_3 (.in_1(A2), .B(B2), .Selector(selector), .out_4(out_2));
  _8_bit_MUX_main main_4 (.in_1(A3), .B(B3), .Selector(selector), .out_4(out_3));

  // Notes on the sheet:
  //   2x1 MUX
  //   2x1 MUX
  //   2x1 MUX
  //   2x1 MUX
endmodule

module _2_1_mux (
  input  in_1,
  input  B,
  input  Selector,
  output out_4
);

  wire and_1_out, and_2_out, not_1_out;

  not not_1 (not_1_out, Selector);
  and and_1 (and_1_out, in_1, not_1_out);
  and and_2 (and_2_out, B, Selector);
  or or_1 (out_4, and_1_out, and_2_out);

  // Notes on the sheet:
  //   A
endmodule

module exchanger (
  input  A3,
  input  in_2,
  input  in_3,
  input  A0,
  input  B3,
  input  in_6,
  input  in_7,
  input  B0,
  input  signal,
  output f3,
  output out_11,
  output out_12,
  output f0,
  output s3,
  output out_15,
  output out_16,
  output s0
);

  wire not_1_out;

  _8_bit_mux u_8_bit_mux_1 (
    .A3(A3), .A2(in_2), .A1(in_3), .A0(A0), .B3(B3), .B2(in_6), .B1(in_7), .B0(B0), .selector(signal),
    .out_3(f3), .out_2(out_11), .out_1(out_12), .out_0(f0));
  _8_bit_mux u_8_bit_mux_2 (
    .A3(A3), .A2(in_2), .A1(in_3), .A0(A0), .B3(B3), .B2(in_6), .B1(in_7), .B0(B0), .selector(not_1_out),
    .out_3(s3), .out_2(out_15), .out_1(out_16), .out_0(s0));
  not not_1 (not_1_out, signal);
endmodule

module add___sub_manager (
  input  add,
  input  sub,
  output enable,
  output control
);

  wire not_1_out;

  not not_1 (not_1_out, add);
  or or_1 (enable, add, sub);
  and and_1 (control, not_1_out, sub);
endmodule

module devider (
  input  A0,
  input  A1,
  input  A2,
  input  A3,
  input  B0,
  input  B1,
  input  B2,
  input  B3,
  input  enable,
  output R0,
  output R1,
  output R2,
  output R3,
  output D0,
  output D1,
  output D2,
  output D3
);

  wire n4_bit_comparaor_1_out_9, n4_bit_comparaor_1_s, n4_bit_comparaor_2_out_9, n4_bit_comparaor_2_s,
       n4_bit_comparaor_3_out_9, n4_bit_comparaor_3_s, n4_bit_comparaor_4_out_9, n4_bit_comparaor_4_s,
       n8_bit_mux_1_out_10, n8_bit_mux_1_out_11, n8_bit_mux_1_out_12, n8_bit_mux_1_out_13,
       n8_bit_mux_2_out_10, n8_bit_mux_2_out_11, n8_bit_mux_2_out_12, n8_bit_mux_2_out_13,
       n8_bit_mux_3_out_10, n8_bit_mux_3_out_11, n8_bit_mux_3_out_12, n8_bit_mux_3_out_13,
       n8_bit_mux_4_out_10, n8_bit_mux_4_out_11, n8_bit_mux_4_out_12, n8_bit_mux_4_out_13,
       unsigned_4_bit_subtractor_1_d0, unsigned_4_bit_subtractor_1_d1, unsigned_4_bit_subtractor_1_d2,
       unsigned_4_bit_subtractor_1_d3, unsigned_4_bit_subtractor_1_sign, unsigned_4_bit_subtractor_2_d0,
       unsigned_4_bit_subtractor_2_d1, unsigned_4_bit_subtractor_2_d2, unsigned_4_bit_subtractor_2_d3,
       unsigned_4_bit_subtractor_2_sign, unsigned_4_bit_subtractor_3_d0, unsigned_4_bit_subtractor_3_d1,
       unsigned_4_bit_subtractor_3_d2, unsigned_4_bit_subtractor_3_d3, unsigned_4_bit_subtractor_3_sign,
       unsigned_4_bit_subtractor_4_d0, unsigned_4_bit_subtractor_4_d1, unsigned_4_bit_subtractor_4_d2,
       unsigned_4_bit_subtractor_4_d3, unsigned_4_bit_subtractor_4_sign;

  Unsigned_4_bit_Subtractor unsigned_4_bit_subtractor_1 (
    .A3(A3), .A2(1'b0), .A1(1'b0), .A0(1'b0), .B3(B3), .B2(B2), .B1(B1), .B0(B0), .BORROW_IN_0(1'b0),
    .Sign(unsigned_4_bit_subtractor_1_sign), .D3(unsigned_4_bit_subtractor_1_d3),
    .D2(unsigned_4_bit_subtractor_1_d2), .D1(unsigned_4_bit_subtractor_1_d1),
    .D0(unsigned_4_bit_subtractor_1_d0));
  _4_bit_Comparaor u_4_bit_comparaor_1 (
    .A0(A3), .A1(1'b0), .A2(1'b0), .A3(1'b0), .B0(B0), .B1(B1), .B2(B2), .B3(B3),
    .out_9(n4_bit_comparaor_1_out_9), .S(n4_bit_comparaor_1_s));
  _8_bit_MUX u_8_bit_mux_1 (
    .A0(A3), .A1(1'b0), .A2(1'b0), .A3(1'b0), .B0(unsigned_4_bit_subtractor_1_d0),
    .B1(unsigned_4_bit_subtractor_1_d1), .B2(unsigned_4_bit_subtractor_1_d2),
    .B3(unsigned_4_bit_subtractor_1_d3), .selector(n4_bit_comparaor_1_out_9), .out_10(n8_bit_mux_1_out_10),
    .out_11(n8_bit_mux_1_out_11), .out_12(n8_bit_mux_1_out_12), .out_13(n8_bit_mux_1_out_13));
  _4_bit_Comparaor u_4_bit_comparaor_2 (
    .A0(A2), .A1(n8_bit_mux_1_out_10), .A2(n8_bit_mux_1_out_11), .A3(n8_bit_mux_1_out_12), .B0(B0), .B1(B1),
    .B2(B2), .B3(B3), .out_9(n4_bit_comparaor_2_out_9), .S(n4_bit_comparaor_2_s));
  Unsigned_4_bit_Subtractor unsigned_4_bit_subtractor_2 (
    .A3(A2), .A2(A3), .A1(1'b0), .A0(1'b0), .B3(B3), .B2(B2), .B1(B1), .B0(B0), .BORROW_IN_0(1'b0),
    .Sign(unsigned_4_bit_subtractor_2_sign), .D3(unsigned_4_bit_subtractor_2_d3),
    .D2(unsigned_4_bit_subtractor_2_d2), .D1(unsigned_4_bit_subtractor_2_d1),
    .D0(unsigned_4_bit_subtractor_2_d0));
  _8_bit_MUX u_8_bit_mux_2 (
    .A0(A2), .A1(n8_bit_mux_1_out_10), .A2(1'b0), .A3(1'b0), .B0(unsigned_4_bit_subtractor_2_d0),
    .B1(unsigned_4_bit_subtractor_2_d1), .B2(unsigned_4_bit_subtractor_2_d2),
    .B3(unsigned_4_bit_subtractor_2_d3), .selector(n4_bit_comparaor_2_out_9), .out_10(n8_bit_mux_2_out_10),
    .out_11(n8_bit_mux_2_out_11), .out_12(n8_bit_mux_2_out_12), .out_13(n8_bit_mux_2_out_13));
  _4_bit_Comparaor u_4_bit_comparaor_3 (
    .A0(A1), .A1(n8_bit_mux_2_out_10), .A2(n8_bit_mux_2_out_11), .A3(n8_bit_mux_2_out_12), .B0(B0), .B1(B1),
    .B2(B2), .B3(B3), .out_9(n4_bit_comparaor_3_out_9), .S(n4_bit_comparaor_3_s));
  Unsigned_4_bit_Subtractor unsigned_4_bit_subtractor_3 (
    .A3(n8_bit_mux_2_out_12), .A2(n8_bit_mux_2_out_11), .A1(n8_bit_mux_2_out_10), .A0(A1), .B3(B3), .B2(B2),
    .B1(B1), .B0(B0), .BORROW_IN_0(1'b0), .Sign(unsigned_4_bit_subtractor_3_sign),
    .D3(unsigned_4_bit_subtractor_3_d3), .D2(unsigned_4_bit_subtractor_3_d2),
    .D1(unsigned_4_bit_subtractor_3_d1), .D0(unsigned_4_bit_subtractor_3_d0));
  _8_bit_MUX u_8_bit_mux_3 (
    .A0(A1), .A1(n8_bit_mux_2_out_10), .A2(n8_bit_mux_2_out_11), .A3(n8_bit_mux_2_out_12),
    .B0(unsigned_4_bit_subtractor_3_d0), .B1(unsigned_4_bit_subtractor_3_d1),
    .B2(unsigned_4_bit_subtractor_3_d2), .B3(unsigned_4_bit_subtractor_3_d3),
    .selector(n4_bit_comparaor_3_out_9), .out_10(n8_bit_mux_3_out_10), .out_11(n8_bit_mux_3_out_11),
    .out_12(n8_bit_mux_3_out_12), .out_13(n8_bit_mux_3_out_13));
  _4_bit_Comparaor u_4_bit_comparaor_4 (
    .A0(A0), .A1(n8_bit_mux_3_out_10), .A2(n8_bit_mux_3_out_11), .A3(n8_bit_mux_3_out_12), .B0(B0), .B1(B1),
    .B2(B2), .B3(B3), .out_9(n4_bit_comparaor_4_out_9), .S(n4_bit_comparaor_4_s));
  Unsigned_4_bit_Subtractor unsigned_4_bit_subtractor_4 (
    .A3(n8_bit_mux_3_out_12), .A2(n8_bit_mux_3_out_11), .A1(n8_bit_mux_3_out_10), .A0(A0), .B3(B3), .B2(B2),
    .B1(B1), .B0(B0), .BORROW_IN_0(1'b0), .Sign(unsigned_4_bit_subtractor_4_sign),
    .D3(unsigned_4_bit_subtractor_4_d3), .D2(unsigned_4_bit_subtractor_4_d2),
    .D1(unsigned_4_bit_subtractor_4_d1), .D0(unsigned_4_bit_subtractor_4_d0));
  _8_bit_MUX u_8_bit_mux_4 (
    .A0(A0), .A1(n8_bit_mux_3_out_10), .A2(n8_bit_mux_3_out_11), .A3(n8_bit_mux_3_out_12),
    .B0(unsigned_4_bit_subtractor_4_d0), .B1(unsigned_4_bit_subtractor_4_d1),
    .B2(unsigned_4_bit_subtractor_4_d2), .B3(unsigned_4_bit_subtractor_4_d3),
    .selector(n4_bit_comparaor_4_out_9), .out_10(n8_bit_mux_4_out_10), .out_11(n8_bit_mux_4_out_11),
    .out_12(n8_bit_mux_4_out_12), .out_13(n8_bit_mux_4_out_13));
  and and_1 (R0, n8_bit_mux_4_out_10, enable);
  and and_2 (R2, n8_bit_mux_4_out_12, enable);
  and and_3 (R3, n8_bit_mux_4_out_13, enable);
  and and_4 (D0, enable, n4_bit_comparaor_4_out_9);
  and and_5 (R1, enable, n8_bit_mux_4_out_11);
  and and_6 (D1, enable, n4_bit_comparaor_3_out_9);
  and and_7 (D2, enable, n4_bit_comparaor_2_out_9);
  and and_8 (D3, enable, n4_bit_comparaor_1_out_9);

  // Notes on the sheet:
  //   A1
  //   A2
  //   A3
  //   B0
  //   B1
  //   B2
  //   B3
  //   A0
  //   SUBT
  //   COMPAR
  //   L OR E
  //   A3
  //   A3
  //   A2
  //   COMP2
  //   L OR E
  //   SUB2
  //   MUX2
  //   COMP3
  //   SUB3
  //   MUX3
  //   COMP4
  //   MUX4
endmodule

module Zero_flag (
  input  M0,
  input  a,
  input  b,
  input  c,
  input  d,
  input  e,
  input  f,
  input  M7,
  output x
);

  wire or_1_out, or_2_out, or_3_out, or_4_out, or_5_out, or_6_out, or_7_out;

  or or_1 (or_1_out, M0, a);
  or or_2 (or_2_out, b, c);
  or or_3 (or_3_out, d, e);
  or or_4 (or_4_out, f, M7);
  or or_5 (or_5_out, or_1_out, or_2_out);
  or or_6 (or_6_out, or_5_out, or_7_out);
  or or_7 (or_7_out, or_3_out, or_4_out);
  not not_1 (x, or_6_out);
endmodule

module last_dividor (
  input  A0,
  input  A1,
  input  A2,
  input  A3,
  input  B0,
  input  B1,
  input  B2,
  input  B3,
  input  enable,
  output R0,
  output R1,
  output R2,
  output R3,
  output D0,
  output D1,
  output D2,
  output D3
);

  wire n4_bit_comparaor_1_out_9, n4_bit_comparaor_1_s, n4_bit_comparaor_2_out_9, n4_bit_comparaor_2_s,
       n4_bit_comparaor_3_out_9, n4_bit_comparaor_3_s, n4_bit_comparaor_4_out_9, n4_bit_comparaor_4_s,
       n8_bit_mux_1_out_10, n8_bit_mux_1_out_11, n8_bit_mux_1_out_12, n8_bit_mux_1_out_13,
       n8_bit_mux_2_out_10, n8_bit_mux_2_out_11, n8_bit_mux_2_out_12, n8_bit_mux_2_out_13,
       n8_bit_mux_3_out_10, n8_bit_mux_3_out_11, n8_bit_mux_3_out_12, n8_bit_mux_3_out_13,
       n8_bit_mux_4_out_10, n8_bit_mux_4_out_11, n8_bit_mux_4_out_12, n8_bit_mux_4_out_13,
       unsigned_4_bit_subtractor_1_d0, unsigned_4_bit_subtractor_1_d1, unsigned_4_bit_subtractor_1_d2,
       unsigned_4_bit_subtractor_1_d3, unsigned_4_bit_subtractor_1_sign, unsigned_4_bit_subtractor_2_d0,
       unsigned_4_bit_subtractor_2_d1, unsigned_4_bit_subtractor_2_d2, unsigned_4_bit_subtractor_2_d3,
       unsigned_4_bit_subtractor_2_sign, unsigned_4_bit_subtractor_3_d0, unsigned_4_bit_subtractor_3_d1,
       unsigned_4_bit_subtractor_3_d2, unsigned_4_bit_subtractor_3_d3, unsigned_4_bit_subtractor_3_sign,
       unsigned_4_bit_subtractor_4_d0, unsigned_4_bit_subtractor_4_d1, unsigned_4_bit_subtractor_4_d2,
       unsigned_4_bit_subtractor_4_d3, unsigned_4_bit_subtractor_4_sign;

  Unsigned_4_bit_Subtractor unsigned_4_bit_subtractor_1 (
    .A3(1'b0), .A2(1'b0), .A1(1'b0), .A0(A3), .B3(B3), .B2(B2), .B1(B1), .B0(B0), .BORROW_IN_0(1'b0),
    .Sign(unsigned_4_bit_subtractor_1_sign), .D3(unsigned_4_bit_subtractor_1_d3),
    .D2(unsigned_4_bit_subtractor_1_d2), .D1(unsigned_4_bit_subtractor_1_d1),
    .D0(unsigned_4_bit_subtractor_1_d0));
  _4_bit_Comparaor u_4_bit_comparaor_1 (
    .A0(A3), .A1(1'b0), .A2(1'b0), .A3(1'b0), .B0(B0), .B1(B1), .B2(B2), .B3(B3),
    .out_9(n4_bit_comparaor_1_out_9), .S(n4_bit_comparaor_1_s));
  _8_bit_MUX u_8_bit_mux_1 (
    .A0(A3), .A1(1'b0), .A2(1'b0), .A3(1'b0), .B0(unsigned_4_bit_subtractor_1_d0),
    .B1(unsigned_4_bit_subtractor_1_d1), .B2(unsigned_4_bit_subtractor_1_d2),
    .B3(unsigned_4_bit_subtractor_1_d3), .selector(n4_bit_comparaor_1_out_9), .out_10(n8_bit_mux_1_out_10),
    .out_11(n8_bit_mux_1_out_11), .out_12(n8_bit_mux_1_out_12), .out_13(n8_bit_mux_1_out_13));
  _4_bit_Comparaor u_4_bit_comparaor_2 (
    .A0(A2), .A1(n8_bit_mux_1_out_10), .A2(n8_bit_mux_1_out_11), .A3(n8_bit_mux_1_out_12), .B0(B0), .B1(B1),
    .B2(B2), .B3(B3), .out_9(n4_bit_comparaor_2_out_9), .S(n4_bit_comparaor_2_s));
  Unsigned_4_bit_Subtractor unsigned_4_bit_subtractor_2 (
    .A3(1'b0), .A2(1'b0), .A1(A3), .A0(A2), .B3(B3), .B2(B2), .B1(B1), .B0(B0), .BORROW_IN_0(1'b0),
    .Sign(unsigned_4_bit_subtractor_2_sign), .D3(unsigned_4_bit_subtractor_2_d3),
    .D2(unsigned_4_bit_subtractor_2_d2), .D1(unsigned_4_bit_subtractor_2_d1),
    .D0(unsigned_4_bit_subtractor_2_d0));
  _8_bit_MUX u_8_bit_mux_2 (
    .A0(A2), .A1(n8_bit_mux_1_out_10), .A2(1'b0), .A3(1'b0), .B0(unsigned_4_bit_subtractor_2_d0),
    .B1(unsigned_4_bit_subtractor_2_d1), .B2(unsigned_4_bit_subtractor_2_d2),
    .B3(unsigned_4_bit_subtractor_2_d3), .selector(n4_bit_comparaor_2_out_9), .out_10(n8_bit_mux_2_out_10),
    .out_11(n8_bit_mux_2_out_11), .out_12(n8_bit_mux_2_out_12), .out_13(n8_bit_mux_2_out_13));
  _4_bit_Comparaor u_4_bit_comparaor_3 (
    .A0(A1), .A1(n8_bit_mux_2_out_10), .A2(n8_bit_mux_2_out_11), .A3(n8_bit_mux_2_out_12), .B0(B0), .B1(B1),
    .B2(B2), .B3(B3), .out_9(n4_bit_comparaor_3_out_9), .S(n4_bit_comparaor_3_s));
  Unsigned_4_bit_Subtractor unsigned_4_bit_subtractor_3 (
    .A3(n8_bit_mux_2_out_12), .A2(n8_bit_mux_2_out_11), .A1(n8_bit_mux_2_out_10), .A0(A1), .B3(B3), .B2(B2),
    .B1(B1), .B0(B0), .BORROW_IN_0(1'b0), .Sign(unsigned_4_bit_subtractor_3_sign),
    .D3(unsigned_4_bit_subtractor_3_d3), .D2(unsigned_4_bit_subtractor_3_d2),
    .D1(unsigned_4_bit_subtractor_3_d1), .D0(unsigned_4_bit_subtractor_3_d0));
  _8_bit_MUX u_8_bit_mux_3 (
    .A0(A1), .A1(n8_bit_mux_2_out_10), .A2(n8_bit_mux_2_out_11), .A3(n8_bit_mux_2_out_12),
    .B0(unsigned_4_bit_subtractor_3_d0), .B1(unsigned_4_bit_subtractor_3_d1),
    .B2(unsigned_4_bit_subtractor_3_d2), .B3(unsigned_4_bit_subtractor_3_d3),
    .selector(n4_bit_comparaor_3_out_9), .out_10(n8_bit_mux_3_out_10), .out_11(n8_bit_mux_3_out_11),
    .out_12(n8_bit_mux_3_out_12), .out_13(n8_bit_mux_3_out_13));
  _4_bit_Comparaor u_4_bit_comparaor_4 (
    .A0(A0), .A1(n8_bit_mux_3_out_10), .A2(n8_bit_mux_3_out_11), .A3(n8_bit_mux_3_out_12), .B0(B0), .B1(B1),
    .B2(B2), .B3(B3), .out_9(n4_bit_comparaor_4_out_9), .S(n4_bit_comparaor_4_s));
  Unsigned_4_bit_Subtractor unsigned_4_bit_subtractor_4 (
    .A3(n8_bit_mux_3_out_12), .A2(n8_bit_mux_3_out_11), .A1(n8_bit_mux_3_out_10), .A0(A0), .B3(B3), .B2(B2),
    .B1(B1), .B0(B0), .BORROW_IN_0(1'b0), .Sign(unsigned_4_bit_subtractor_4_sign),
    .D3(unsigned_4_bit_subtractor_4_d3), .D2(unsigned_4_bit_subtractor_4_d2),
    .D1(unsigned_4_bit_subtractor_4_d1), .D0(unsigned_4_bit_subtractor_4_d0));
  _8_bit_MUX u_8_bit_mux_4 (
    .A0(A0), .A1(n8_bit_mux_3_out_10), .A2(n8_bit_mux_3_out_11), .A3(n8_bit_mux_3_out_12),
    .B0(unsigned_4_bit_subtractor_4_d0), .B1(unsigned_4_bit_subtractor_4_d1),
    .B2(unsigned_4_bit_subtractor_4_d2), .B3(unsigned_4_bit_subtractor_4_d3),
    .selector(n4_bit_comparaor_4_out_9), .out_10(n8_bit_mux_4_out_10), .out_11(n8_bit_mux_4_out_11),
    .out_12(n8_bit_mux_4_out_12), .out_13(n8_bit_mux_4_out_13));
  and and_1 (R0, n8_bit_mux_4_out_10, enable);
  and and_2 (R2, n8_bit_mux_4_out_12, enable);
  and and_3 (R3, n8_bit_mux_4_out_13, enable);
  and and_4 (D0, enable, n4_bit_comparaor_4_out_9);
  and and_5 (R1, enable, n8_bit_mux_4_out_11);
  and and_6 (D1, enable, n4_bit_comparaor_3_out_9);
  and and_7 (D2, enable, n4_bit_comparaor_2_out_9);
  and and_8 (D3, enable, n4_bit_comparaor_1_out_9);

  // Notes on the sheet:
  //   SUBT
  //   COMPAR
  //   L OR E
  //   A3
  //   A3
  //   A2
  //   COMP2
  //   L OR E
  //   SUB2
  //   MUX2
  //   COMP3
  //   SUB3
  //   MUX3
  //   COMP4
  //   MUX4
  //   sub4
endmodule

module ALU (
  input  signal_1,
  input  signal_2,
  input  A_sign,
  input  A3,
  input  in_5,
  input  in_6,
  input  A0,
  input  B_sign,
  input  B3,
  input  in_10,
  input  in_11,
  input  B0,
  output P9,
  output P8,
  output P7,
  output P6,
  output P5,
  output P4,
  output P3,
  output P2,
  output P1,
  output P0,
  output div_by_0,
  output sign,
  output Zero
);

  wire add_sub_manager_1_control, add_sub_manager_1_enable, adder_subtractor_1_s0___d0,
       adder_subtractor_1_s1___d1, adder_subtractor_1_s2___d2, adder_subtractor_1_s3___d3,
       adder_subtractor_1_s4, adder_subtractor_1_sign, exchanger_1_f0, exchanger_1_f3, exchanger_1_out_11,
       exchanger_1_out_12, exchanger_1_out_15, exchanger_1_out_16, exchanger_1_s0, exchanger_1_s3,
       last_dividor_1_d0, last_dividor_1_d1, last_dividor_1_d2, last_dividor_1_d3, multi_1_m0, multi_1_m1,
       multi_1_m2, multi_1_m3, multi_1_m4, multi_1_m5, multi_1_m6, multi_1_m7, not_1_out, op_selector_1_add,
       op_selector_1_div, op_selector_1_multi, op_selector_1_sub, or_1_out, or_2_out, or_3_out, or_5_out,
       or_6_out, or_7_out, or_8_out, or_9_out, or_10_out, or_11_out, or_12_out, or_13_out,
       sign_manager_1_exchange, sign_manager_1_out_1, sign_manager_1_out_2, sign_manager_1_sign;

  sign_manager sign_manager_1 (
    .signal_1(signal_1), .signal_2(signal_2), .A_sign(A_sign), .B_sign(B_sign), .out_1(sign_manager_1_out_1),
    .out_2(sign_manager_1_out_2), .sign(sign_manager_1_sign), .exchange(sign_manager_1_exchange));
  or or_1 (or_1_out, B3, in_10);
  or or_2 (or_2_out, in_11, B0);
  not not_1 (not_1_out, or_3_out);
  or or_3 (or_3_out, or_1_out, or_2_out);
  and and_1 (div_by_0, not_1_out, op_selector_1_div);
  op_selector op_selector_1 (
    .out_1(sign_manager_1_out_1), .out_2(sign_manager_1_out_2), .Add(op_selector_1_add),
    .sub(op_selector_1_sub), .multi(op_selector_1_multi), .div(op_selector_1_div));
  or or_4 (sign, sign_manager_1_sign, adder_subtractor_1_sign);
  add___sub_manager add_sub_manager_1 (
    .add(op_selector_1_add), .sub(op_selector_1_sub), .enable(add_sub_manager_1_enable),
    .control(add_sub_manager_1_control));
  exchanger exchanger_1 (
    .A3(A3), .in_2(in_5), .in_3(in_6), .A0(A0), .B3(B3), .in_6(in_10), .in_7(in_11), .B0(B0),
    .signal(sign_manager_1_exchange), .f3(exchanger_1_f3), .out_11(exchanger_1_out_11),
    .out_12(exchanger_1_out_12), .f0(exchanger_1_f0), .s3(exchanger_1_s3), .out_15(exchanger_1_out_15),
    .out_16(exchanger_1_out_16), .s0(exchanger_1_s0));
  last_dividor last_dividor_1 (
    .A0(A0), .A1(in_6), .A2(in_5), .A3(A3), .B0(B0), .B1(in_11), .B2(in_10), .B3(B3),
    .enable(op_selector_1_div), .D0(last_dividor_1_d0), .D1(last_dividor_1_d1), .D2(last_dividor_1_d2),
    .D3(last_dividor_1_d3));  // open: R0, R1, R2, R3
  Adder___Subtractor adder_subtractor_1 (
    .A3(exchanger_1_f3), .A2(exchanger_1_out_11), .A1(exchanger_1_out_12), .A0(exchanger_1_f0),
    .B3(exchanger_1_s3), .B2(exchanger_1_out_15), .B1(exchanger_1_out_16), .B0(exchanger_1_s0),
    .Control(add_sub_manager_1_control), .Enable(add_sub_manager_1_enable), .Sign(adder_subtractor_1_sign),
    .S4(adder_subtractor_1_s4), .S3___D3(adder_subtractor_1_s3___d3), .S2___D2(adder_subtractor_1_s2___d2),
    .S1___D1(adder_subtractor_1_s1___d1), .S0___D0(adder_subtractor_1_s0___d0));
  multi multi_1 (
    .A3(A3), .A2(in_5), .A1(in_6), .A0(A0), .B3(B3), .B2(in_10), .B1(in_11), .B0(B0),
    .Enable(op_selector_1_multi), .M0(multi_1_m0), .m1(multi_1_m1), .M2(multi_1_m2), .M3(multi_1_m3),
    .M4(multi_1_m4), .M5(multi_1_m5), .M6(multi_1_m6), .M7(multi_1_m7));
  or or_5 (or_5_out, adder_subtractor_1_s2___d2, multi_1_m2);
  or or_6 (or_6_out, multi_1_m1, adder_subtractor_1_s1___d1);
  or or_7 (or_7_out, or_6_out, last_dividor_1_d1);
  or or_8 (or_8_out, last_dividor_1_d0, adder_subtractor_1_s0___d0);
  or or_9 (or_9_out, adder_subtractor_1_s4, multi_1_m4);
  or or_10 (or_10_out, adder_subtractor_1_s3___d3, multi_1_m3);
  or or_11 (or_11_out, or_10_out, last_dividor_1_d3);
  or or_12 (or_12_out, or_5_out, last_dividor_1_d2);
  or or_13 (or_13_out, or_8_out, multi_1_m0);
  Zero_flag zero_flag_1 (
    .M0(multi_1_m7), .a(multi_1_m6), .b(multi_1_m5), .c(or_9_out), .d(or_11_out), .e(or_7_out),
    .f(or_13_out), .M7(or_12_out), .x(Zero));
  Binary_To_BCD_main main_1 (
    .B7(multi_1_m7), .B6(multi_1_m6), .B5(multi_1_m5), .B4(or_9_out), .B3(or_11_out), .B2(or_12_out),
    .B1(or_7_out), .B0(or_13_out), .p9(P9), .p8(P8), .p7(P7), .p6(P6), .p5(P5), .p4(P4), .p3(P3), .p2(P2),
    .p1(P1), .p0(P0));
endmodule
