// Logisim project last dividor.circ as structural Verilog: 13 circuits, main circuit 1-bit Half Adder
// HA
module _1_bit_Half_Adder (
  input  in_1,
  input  in_2,
  output out_3,
  output out_4
);

  xor xor_1 (out_3, in_1, in_2);
  and and_1 (out_4, in_1, in_2);
endmodule

module _1_bit_Full_Adder (
  input  An,
  input  Bn,
  input  C_in_n,
  output out_4,
  output out_5
);

  wire n1_bit_half_adder_1_out_3, n1_bit_half_adder_1_out_4, n1_bit_half_adder_2_out_4;

  _1_bit_Half_Adder u_1_bit_half_adder_1 (
    .in_1(An), .in_2(Bn), .out_3(n1_bit_half_adder_1_out_3), .out_4(n1_bit_half_adder_1_out_4));
  _1_bit_Half_Adder u_1_bit_half_adder_2 (
    .in_1(n1_bit_half_adder_1_out_3), .in_2(C_in_n), .out_3(out_4), .out_4(n1_bit_half_adder_2_out_4));
  or or_1 (out_5, n1_bit_half_adder_2_out_4, n1_bit_half_adder_1_out_4);
endmodule

module Unsigned_4_bit_Full_Adder (
  input  A3,
  input  A2,
  input  A1,
  input  A0,
  input  B3,
  input  B2,
  input  B1,
  input  B0,
  input  C_in_1___0,
  output S4,
  output S3,
  output S2,
  output S1,
  output S0
);

  wire n1_bit_full_adder_2_out_5, n1_bit_full_adder_3_out_5, n1_bit_full_adder_4_out_5;

  _1_bit_Full_Adder u_1_bit_full_adder_1 (.An(A3), .Bn(B3), .C_in_n(n1_bit_full_adder_2_out_5), .out_4(S3), .out_5(S4));
  _1_bit_Full_Adder u_1_bit_full_adder_2 (
    .An(A2), .Bn(B2), .C_in_n(n1_bit_full_adder_3_out_5), .out_4(S2), .out_5(n1_bit_full_adder_2_out_5));
  _1_bit_Full_Adder u_1_bit_full_adder_3 (
    .An(A1), .Bn(B1), .C_in_n(n1_bit_full_adder_4_out_5), .out_4(S1), .out_5(n1_bit_full_adder_3_out_5));
  _1_bit_Full_Adder u_1_bit_full_adder_4 (
    .An(A0), .Bn(B0), .C_in_n(C_in_1___0), .out_4(S0), .out_5(n1_bit_full_adder_4_out_5));

  // Notes on the sheet:
  //   MSB
  //   LSB
  //   MSB
  //   LSB
  //   MSB
  //   LSB
endmodule

module _1_bit_Half_Subtractor (
  input  An,
  input  Bn,
  output Difference,
  output Borrow
);

  wire not_1_out;

  not not_1 (not_1_out, An);
  xor xor_1 (Difference, An, Bn);
  and and_1 (Borrow, not_1_out, Bn);
endmodule

module _1_bit_Full_Subtractor (
  input  An,
  input  Bn,
  input  B_in_n,
  output Borrow,
  output Difference
);

  wire Half_Subtractor_2_borrow, Half_Subtractor_borrow, Half_Subtractor_difference;

  _1_bit_Half_Subtractor Half_Subtractor (
    .An(An), .Bn(Bn), .Difference(Half_Subtractor_difference), .Borrow(Half_Subtractor_borrow));
  _1_bit_Half_Subtractor Half_Subtractor_2 (
    .An(Half_Subtractor_difference), .Bn(B_in_n), .Difference(Difference), .Borrow(Half_Subtractor_2_borrow));
  or or_1 (Borrow, Half_Subtractor_2_borrow, Half_Subtractor_borrow);
endmodule

module Unsigned_4_bit_Subtractor (
  input  A3,
  input  A2,
  input  A1,
  input  A0,
  input  B3,
  input  B2,
  input  B1,
  input  B0,
  input  BORROW_IN_0,
  output Sign,
  output D3,
  output D2,
  output D1,
  output D0
);

  wire and_1_out, and_2_out, and_3_out, and_4_out, and_5_out, and_6_out, and_7_out, and_8_out,
       n1_bit_full_subtractor_1_difference, n1_bit_full_subtractor_2_borrow,
       n1_bit_full_subtractor_2_difference, n1_bit_full_subtractor_3_borrow,
       n1_bit_full_subtractor_3_difference, n1_bit_full_subtractor_4_borrow,
       n1_bit_full_subtractor_4_difference, n2_s_complement_1_out_5, n2_s_complement_1_out_6,
       n2_s_complement_1_out_7, n2_s_complement_1_out_8, not_1_out, not_2_out, not_3_out, not_4_out;

  _1_bit_Full_Subtractor u_1_bit_full_subtractor_1 (
    .An(A3), .Bn(B3), .Borrow(Sign), .Difference(n1_bit_full_subtractor_1_difference),
    .B_in_n(n1_bit_full_subtractor_2_borrow));
  _1_bit_Full_Subtractor u_1_bit_full_subtractor_2 (
    .An(A2), .Bn(B2), .Borrow(n1_bit_full_subtractor_2_borrow),
    .Difference(n1_bit_full_subtractor_2_difference), .B_in_n(n1_bit_full_subtractor_3_borrow));
  _1_bit_Full_Subtractor u_1_bit_full_subtractor_3 (
    .An(A1), .Bn(B1), .Borrow(n1_bit_full_subtractor_3_borrow),
    .Difference(n1_bit_full_subtractor_3_difference), .B_in_n(n1_bit_full_subtractor_4_borrow));
  _1_bit_Full_Subtractor u_1_bit_full_subtractor_4 (
    .An(A0), .Bn(B0), .Borrow(n1_bit_full_subtractor_4_borrow),
    .Difference(n1_bit_full_subtractor_4_difference), .B_in_n(BORROW_IN_0));
  _2_s_Complement u_2_s_complement_1 (
    .in_1(n1_bit_full_subtractor_1_difference), .in_2(n1_bit_full_subtractor_2_difference),
    .in_3(n1_bit_full_subtractor_3_difference), .in_4(n1_bit_full_subtractor_4_difference),
    .out_5(n2_s_complement_1_out_5), .out_6(n2_s_complement_1_out_6), .out_7(n2_s_complement_1_out_7),
    .out_8(n2_s_complement_1_out_8));
  not not_1 (not_1_out, Sign);
  and and_1 (and_1_out, not_1_out, n1_bit_full_subtractor_1_difference);
  not not_2 (not_2_out, Sign);
  and and_2 (and_2_out, not_2_out, n1_bit_full_subtractor_2_difference);
  not not_3 (not_3_out, Sign);
  and and_3 (and_3_out, not_3_out, n1_bit_full_subtractor_3_difference);
  not not_4 (not_4_out, Sign);
  and and_4 (and_4_out, not_4_out, n1_bit_full_subtractor_4_difference);
  and and_5 (and_5_out, Sign, n2_s_complement_1_out_5);
  and and_6 (and_6_out, Sign, n2_s_complement_1_out_6);
  and and_7 (and_7_out, Sign, n2_s_complement_1_out_7);
  and and_8 (and_8_out, Sign, n2_s_complement_1_out_8);
  or or_1 (D3, and_1_out, and_5_out);
  or or_2 (D2, and_2_out, and_6_out);
  or or_3 (D1, and_3_out, and_7_out);
  or or_4 (D0, and_4_out, and_8_out);

  // Notes on the sheet:
  //   MSB
  //   LSB
  //   MSB
  //   LSB
  //   MSB
  //   LSB
endmodule

module _2_s_Complement (
  input  in_1,
  input  in_2,
  input  in_3,
  input  in_4,
  output out_5,
  output out_6,
  output out_7,
  output out_8
);

  wire not_1_out, not_2_out, not_3_out, not_4_out;

  not not_1 (not_1_out, in_1);
  not not_2 (not_2_out, in_2);
  not not_3 (not_3_out, in_3);
  not not_4 (not_4_out, in_4);
  Unsigned_4_bit_Full_Adder unsigned_4_bit_full_adder_1 (
    .A3(not_1_out), .A2(not_2_out), .A1(not_3_out), .A0(not_4_out), .B3(1'b0), .B2(1'b0), .B1(1'b0),
    .B0(1'b0), .C_in_1___0(1'b1), .S3(out_5), .S2(out_6), .S1(out_7), .S0(out_8));  // open: S4
endmodule

module Adder___Subtractor (
  input  Control,
  input  A3,
  input  A2,
  input  A1,
  input  A0,
  input  B3,
  input  B2,
  input  B1,
  input  B0,
  input  Enable,
  output Sign,
  output D3,
  output D2,
  output D1,
  output D0
);

  wire Adder_Case_out, and_1_out, and_2_out, and_3_out, and_4_out, and_5_out, and_6_out, and_7_out,
       and_8_out, and_9_out, and_10_out, and_11_out, and_12_out, and_13_out, and_14_out, and_15_out,
       and_16_out, and_17_out, n1_bit_full_adder_1_out_4, n1_bit_full_adder_1_out_5,
       n1_bit_full_adder_2_out_4, n1_bit_full_adder_2_out_5, n1_bit_full_adder_3_out_4,
       n1_bit_full_adder_3_out_5, n1_bit_full_adder_4_out_4, n1_bit_full_adder_4_out_5,
       n2_s_complement_1_out_5, n2_s_complement_1_out_6, n2_s_complement_1_out_7, n2_s_complement_1_out_8,
       not_1_out, not_2_out, not_3_out, not_4_out, not_5_out, not_6_out, or_2_out, Subtractor_Case_out,
       xor_1_out, xor_2_out, xor_3_out, xor_4_out;

  and and_1 (and_1_out, A3, Enable);
  and and_2 (and_2_out, A2, Enable);
  and and_3 (and_3_out, A1, Enable);
  and and_4 (and_4_out, A0, Enable);
  and and_5 (and_5_out, B3, Enable);
  and and_6 (and_6_out, B2, Enable);
  and and_7 (and_7_out, B1, Enable);
  and and_8 (and_8_out, B0, Enable);
  xor xor_1 (xor_1_out, and_5_out, Control);
  xor xor_2 (xor_2_out, and_6_out, Control);
  xor xor_3 (xor_3_out, and_7_out, Control);
  xor xor_4 (xor_4_out, and_8_out, Control);
  _1_bit_Full_Adder u_1_bit_full_adder_1 (
    .An(and_1_out), .Bn(xor_1_out), .C_in_n(n1_bit_full_adder_2_out_5), .out_4(n1_bit_full_adder_1_out_4),
    .out_5(n1_bit_full_adder_1_out_5));
  _1_bit_Full_Adder u_1_bit_full_adder_2 (
    .An(and_2_out), .Bn(xor_2_out), .C_in_n(n1_bit_full_adder_3_out_5), .out_4(n1_bit_full_adder_2_out_4),
    .out_5(n1_bit_full_adder_2_out_5));
  _1_bit_Full_Adder u_1_bit_full_adder_3 (
    .An(and_3_out), .Bn(xor_3_out), .C_in_n(n1_bit_full_adder_4_out_5), .out_4(n1_bit_full_adder_3_out_4),
    .out_5(n1_bit_full_adder_3_out_5));
  _1_bit_Full_Adder u_1_bit_full_adder_4 (
    .An(and_4_out), .Bn(xor_4_out), .C_in_n(Control), .out_4(n1_bit_full_adder_4_out_4),
    .out_5(n1_bit_full_adder_4_out_5));
  not not_1 (not_1_out, Control);
  not not_2 (not_2_out, n1_bit_full_adder_1_out_5);
  and Adder_Case (Adder_Case_out, n1_bit_full_adder_1_out_5, not_1_out);
  and Subtractor_Case (Subtractor_Case_out, not_2_out, Control);
  _2_s_Complement u_2_s_complement_1 (
    .in_1(n1_bit_full_adder_1_out_4), .in_2(n1_bit_full_adder_2_out_4), .in_3(n1_bit_full_adder_3_out_4),
    .in_4(n1_bit_full_adder_4_out_4), .out_5(n2_s_complement_1_out_5), .out_6(n2_s_complement_1_out_6),
    .out_7(n2_s_complement_1_out_7), .out_8(n2_s_complement_1_out_8));
  and and_9 (and_9_out, 1'b0, Adder_Case_out);
  or or_1 (Sign, Adder_Case_out, Subtractor_Case_out);
  or or_2 (or_2_out, and_9_out, Subtractor_Case_out);
  not not_3 (not_3_out, or_2_out);
  not not_4 (not_4_out, or_2_out);
  not not_5 (not_5_out, or_2_out);
  not not_6 (not_6_out, or_2_out);
  and and_10 (and_10_out, not_3_out, n1_bit_full_adder_1_out_4);
  and and_11 (and_11_out, not_4_out, n1_bit_full_adder_2_out_4);
  and and_12 (and_12_out, not_5_out, n1_bit_full_adder_3_out_4);
  and and_13 (and_13_out, not_6_out, n1_bit_full_adder_4_out_4);
  or or_3 (D3, and_10_out, and_14_out);
  and and_14 (and_14_out, or_2_out, n2_s_complement_1_out_5);
  or or_4 (D2, and_11_out, and_15_out);
  and and_15 (and_15_out, or_2_out, n2_s_complement_1_out_6);
  or or_5 (D1, and_12_out, and_16_out);
  and and_16 (and_16_out, or_2_out, n2_s_complement_1_out_7);
  or or_6 (D0, and_13_out, and_17_out);
  and and_17 (and_17_out, or_2_out, n2_s_complement_1_out_8);

  // Notes on the sheet:
  //   MSB
  //   LSB
  //   MSB
  //   LSB
endmodule

module MULTIPLIER2 (
  input  A3,
  input  A2,
  input  A1,
  input  A0,
  input  B3,
  input  B2,
  input  B1,
  input  B0,
  output M0,
  output M1,
  output M2,
  output M3,
  output M4,
  output M5,
  output M6,
  output M7
);

  wire and_1_out, and_2_out, and_3_out, and_4_out, and_5_out, and_6_out, and_7_out, and_8_out, and_9_out,
       and_10_out, and_11_out, and_12_out, and_13_out, and_15_out, and_16_out,
       unsigned_4_bit_full_adder_1_s1, unsigned_4_bit_full_adder_1_s2, unsigned_4_bit_full_adder_1_s3,
       unsigned_4_bit_full_adder_1_s4, unsigned_4_bit_full_adder_2_s1, unsigned_4_bit_full_adder_2_s2,
       unsigned_4_bit_full_adder_2_s3, unsigned_4_bit_full_adder_2_s4;

  and and_1 (and_1_out, B3, A1);
  and and_2 (and_2_out, B2, A1);
  and and_3 (and_3_out, B1, A1);
  and and_4 (and_4_out, B0, A1);
  and and_5 (and_5_out, B0, A2);
  and and_6 (and_6_out, B1, A2);
  and and_7 (and_7_out, B3, A0);
  and and_8 (and_8_out, B2, A2);
  and and_9 (and_9_out, B3, A2);
  and and_10 (and_10_out, B2, A0);
  and and_11 (and_11_out, B1, A0);
  and and_12 (and_12_out, B3, A3);
  Unsigned_4_bit_Full_Adder unsigned_4_bit_full_adder_1 (
    .A3(1'b0), .A2(and_7_out), .A1(and_10_out), .A0(and_11_out), .B3(and_1_out), .B2(and_2_out),
    .B1(and_3_out), .B0(and_4_out), .C_in_1___0(1'b0), .S4(unsigned_4_bit_full_adder_1_s4),
    .S3(unsigned_4_bit_full_adder_1_s3), .S2(unsigned_4_bit_full_adder_1_s2),
    .S1(unsigned_4_bit_full_adder_1_s1), .S0(M1));
  and and_13 (and_13_out, B2, A3);
  and and_14 (M0, B0, A0);
  and and_15 (and_15_out, B1, A3);
  Unsigned_4_bit_Full_Adder unsigned_4_bit_full_adder_2 (
    .A3(unsigned_4_bit_full_adder_1_s4), .A2(unsigned_4_bit_full_adder_1_s3),
    .A1(unsigned_4_bit_full_adder_1_s2), .A0(unsigned_4_bit_full_adder_1_s1), .B3(and_9_out), .B2(and_8_out),
    .B1(and_6_out), .B0(and_5_out), .C_in_1___0(1'b0), .S4(unsigned_4_bit_full_adder_2_s4),
    .S3(unsigned_4_bit_full_adder_2_s3), .S2(unsigned_4_bit_full_adder_2_s2),
    .S1(unsigned_4_bit_full_adder_2_s1), .S0(M2));
  and and_16 (and_16_out, B0, A3);
  Unsigned_4_bit_Full_Adder unsigned_4_bit_full_adder_3 (
    .A3(unsigned_4_bit_full_adder_2_s4), .A2(unsigned_4_bit_full_adder_2_s3),
    .A1(unsigned_4_bit_full_adder_2_s2), .A0(unsigned_4_bit_full_adder_2_s1), .B3(and_12_out),
    .B2(and_13_out), .B1(and_15_out), .B0(and_16_out), .C_in_1___0(1'b0), .S4(M7), .S3(M6), .S2(M5), .S1(M4),
    .S0(M3));

  // Notes on the sheet:
  //   CIN
  //   A1B3
  //   A1B2
  //   A1B1
  //   A2B0
  //   A1B0
  //   A2B1
  //   A2B2
  //   A0B3
  //   A2B3
  //   A0B2
  //   A3B3
  //   A0B1
  //   A3B2
  //   A0B0
  //   A3B1
  //   A3B0
endmodule

module _1_bit_comparator (
  input  Ai,
  input  Bi,
  output L,
  output E,
  output S
);

  wire not_1_out, not_2_out;

  not not_1 (not_1_out, Bi);
  not not_2 (not_2_out, Ai);
  and and_1 (S, Bi, not_2_out);
  and and_2 (L, Ai, not_1_out);
  nor nor_1 (E, L, S);

  // Notes on the sheet:
  //   AiB`i
endmodule

module _4_bit_Comparaor (
  input  A0,
  input  A1,
  input  A2,
  input  A3,
  input  B0,
  input  B1,
  input  B2,
  input  B3,
  output out_9,
  output S
);

  wire and_1_out, and_2_out, and_3_out, and_4_out, and_5_out, and_6_out, and_7_out, and_8_out, and_9_out,
       n1_bit_comparator_1_e, n1_bit_comparator_1_l, n1_bit_comparator_1_s, n1_bit_comparator_2_e,
       n1_bit_comparator_2_l, n1_bit_comparator_2_s, n1_bit_comparator_3_e, n1_bit_comparator_3_l,
       n1_bit_comparator_3_s, n1_bit_comparator_4_e, n1_bit_comparator_4_l, n1_bit_comparator_4_s, or_1_out,
       or_2_out, or_3_out, or_4_out, or_5_out;

  _1_bit_comparator u_1_bit_comparator_1 (
    .Ai(A0), .Bi(B0), .L(n1_bit_comparator_1_l), .E(n1_bit_comparator_1_e), .S(n1_bit_comparator_1_s));
  _1_bit_comparator u_1_bit_comparator_2 (
    .Ai(A1), .Bi(B1), .L(n1_bit_comparator_2_l), .E(n1_bit_comparator_2_e), .S(n1_bit_comparator_2_s));
  _1_bit_comparator u_1_bit_comparator_3 (
    .Ai(A2), .Bi(B2), .L(n1_bit_comparator_3_l), .E(n1_bit_comparator_3_e), .S(n1_bit_comparator_3_s));
  _1_bit_comparator u_1_bit_comparator_4 (
    .Ai(A3), .Bi(B3), .L(n1_bit_comparator_4_l), .E(n1_bit_comparator_4_e), .S(n1_bit_comparator_4_s));
  and and_1 (and_1_out, n1_bit_comparator_3_l, n1_bit_comparator_4_e);
  or or_1 (or_1_out, n1_bit_comparator_4_l, and_1_out);
  and and_2 (and_2_out, n1_bit_comparator_3_e, n1_bit_comparator_4_e);
  and and_3 (and_3_out, n1_bit_comparator_2_e, and_2_out);
  and and_4 (and_4_out, n1_bit_comparator_2_l, and_2_out);
  and and_5 (and_5_out, n1_bit_comparator_1_l, and_3_out);
  and and_6 (and_6_out, n1_bit_comparator_4_e, n1_bit_comparator_3_s);
  or or_2 (or_2_out, or_1_out, and_4_out);
  or or_3 (or_3_out, and_6_out, n1_bit_comparator_4_s);
  and and_7 (and_7_out, and_3_out, n1_bit_comparator_1_e);
  or or_4 (or_4_out, and_5_out, or_2_out);
  and and_8 (and_8_out, n1_bit_comparator_2_s, and_2_out);
  or or_5 (or_5_out, and_8_out, or_3_out);
  and and_9 (and_9_out, n1_bit_comparator_1_s, and_3_out);
  or or_6 (out_9, or_4_out, and_7_out);
  or or_7 (S, and_9_out, or_5_out);

  // Notes on the sheet:
  //   1
  //   2
  //   3
  //   4
  //   l4
  //   L3E4
  //   E3
  //   E4
  //   E2
  //   E3E4
  //   L2
  //   E3E4
  //   E4
  //   S4
  //   L1
  //   E2E3E4
  //   L4+L3E4
  //   E4E3L2
  //   E4S3
  //   E4E3E2L1
  //   E2E3E4
  //   E1
  //   L4+L3E4+L2E4E3
  //   S4+E4S3
  //   S2
  //   E3E4
  //   L(TOTAL)
  //   E(TOTAL)
  //   S2E3E4
  //   S1
  //   E2E3E4
  //   S4+E4S3+S2E3E4
  //   L
  //   E
  //   S1E4E3E2
  //   L OR E
  //   S(TOTAL)
endmodule

module Test (
  input  in_1,
  input  in_2,
  input  in_3,
  input  in_4,
  input  in_5,
  input  in_6,
  input  in_7,
  input  in_8,
  output out_9,
  output out_10
);

  _4_bit_Comparaor u_4_bit_comparaor_1 (
    .A0(in_1), .A1(in_2), .A2(in_3), .A3(in_4), .B0(in_5), .B1(in_6), .B2(in_7), .B3(in_8), .out_9(out_9),
    .S(out_10));
endmodule

module DIVIDERRR (
  input  A0,
  input  A1,
  input  A2,
  input  A3,
  input  B0,
  input  B1,
  input  B2,
  input  B3,
  output R0,
  output R1,
  output R2,
  output R3,
  output D0,
  output D1,
  output D2,
  output D3
);

  wire n4_bit_comparaor_1_s, n4_bit_comparaor_2_s, n4_bit_comparaor_3_s, n4_bit_comparaor_4_s,
       n8_bit_mux_1_out_10, n8_bit_mux_1_out_11, n8_bit_mux_1_out_12, n8_bit_mux_1_out_13,
       n8_bit_mux_2_out_10, n8_bit_mux_2_out_11, n8_bit_mux_2_out_12, n8_bit_mux_2_out_13,
       n8_bit_mux_3_out_10, n8_bit_mux_3_out_11, n8_bit_mux_3_out_12, n8_bit_mux_3_out_13,
       unsigned_4_bit_subtractor_1_d0, unsigned_4_bit_subtractor_1_d1, unsigned_4_bit_subtractor_1_d2,
       unsigned_4_bit_subtractor_1_d3, unsigned_4_bit_subtractor_1_sign, unsigned_4_bit_subtractor_2_d0,
       unsigned_4_bit_subtractor_2_d1, unsigned_4_bit_subtractor_2_d2, unsigned_4_bit_subtractor_2_d3,
       unsigned_4_bit_subtractor_2_sign, unsigned_4_bit_subtractor_3_d0, unsigned_4_bit_subtractor_3_d1,
       unsigned_4_bit_subtractor_3_d2, unsigned_4_bit_subtractor_3_d3, unsigned_4_bit_subtractor_3_sign,
       unsigned_4_bit_subtractor_4_d0, unsigned_4_bit_subtractor_4_d1, unsigned_4_bit_subtractor_4_d2,
       unsigned_4_bit_subtractor_4_d3, unsigned_4_bit_subtractor_4_sign;

  Unsigned_4_bit_Subtractor unsigned_4_bit_subtractor_1 (
    .A3(1'b0), .A2(1'b0), .A1(1'b0), .A0(A3), .B3(B3), .B2(B2), .B1(B1), .B0(B0), .BORROW_IN_0(1'b0),
    .Sign(unsigned_4_bit_subtractor_1_sign), .D3(unsigned_4_bit_subtractor_1_d3),
    .D2(unsigned_4_bit_subtractor_1_d2), .D1(unsigned_4_bit_subtractor_1_d1),
    .D0(unsigned_4_bit_subtractor_1_d0));
  _4_bit_Comparaor u_4_bit_comparaor_1 (
    .A0(A3), .A1(1'b0), .A2(1'b0), .A3(1'b0), .B0(B0), .B1(B1), .B2(B2), .B3(B3), .out_9(D3),
    .S(n4_bit_comparaor_1_s));
  _8_bit_MUX u_8_bit_mux_1 (
    .A0(A3), .A1(1'b0), .A2(1'b0), .A3(1'b0), .B0(unsigned_4_bit_subtractor_1_d0),
    .B1(unsigned_4_bit_subtractor_1_d1), .B2(unsigned_4_bit_subtractor_1_d2),
    .B3(unsigned_4_bit_subtractor_1_d3), .selector(D3), .out_10(n8_bit_mux_1_out_10),
    .out_11(n8_bit_mux_1_out_11), .out_12(n8_bit_mux_1_out_12), .out_13(n8_bit_mux_1_out_13));
  _4_bit_Comparaor u_4_bit_comparaor_2 (
    .A0(A2), .A1(n8_bit_mux_1_out_10), .A2(n8_bit_mux_1_out_11), .A3(n8_bit_mux_1_out_12), .B0(B0), .B1(B1),
    .B2(B2), .B3(B3), .out_9(D2), .S(n4_bit_comparaor_2_s));
  Unsigned_4_bit_Subtractor unsigned_4_bit_subtractor_2 (
    .A3(1'b0), .A2(1'b0), .A1(A3), .A0(A2), .B3(B3), .B2(B2), .B1(B1), .B0(B0), .BORROW_IN_0(1'b0),
    .Sign(unsigned_4_bit_subtractor_2_sign), .D3(unsigned_4_bit_subtractor_2_d3),
    .D2(unsigned_4_bit_subtractor_2_d2), .D1(unsigned_4_bit_subtractor_2_d1),
    .D0(unsigned_4_bit_subtractor_2_d0));
  _8_bit_MUX u_8_bit_mux_2 (
    .A0(A2), .A1(n8_bit_mux_1_out_10), .A2(1'b0), .A3(1'b0), .B0(unsigned_4_bit_subtractor_2_d0),
    .B1(unsigned_4_bit_subtractor_2_d1), .B2(unsigned_4_bit_subtractor_2_d2),
    .B3(unsigned_4_bit_subtractor_2_d3), .selector(D2), .out_10(n8_bit_mux_2_out_10),
    .out_11(n8_bit_mux_2_out_11), .out_12(n8_bit_mux_2_out_12), .out_13(n8_bit_mux_2_out_13));
  _4_bit_Comparaor u_4_bit_comparaor_3 (
    .A0(A1), .A1(n8_bit_mux_2_out_10), .A2(n8_bit_mux_2_out_11), .A3(n8_bit_mux_2_out_12), .B0(B0), .B1(B1),
    .B2(B2), .B3(B3), .out_9(D1), .S(n4_bit_comparaor_3_s));
  Unsigned_4_bit_Subtractor unsigned_4_bit_subtractor_3 (
    .A3(n8_bit_mux_2_out_12), .A2(n8_bit_mux_2_out_11), .A1(n8_bit_mux_2_out_10), .A0(A1), .B3(B3), .B2(B2),
    .B1(B1), .B0(B0), .BORROW_IN_0(1'b0), .Sign(unsigned_4_bit_subtractor_3_sign),
    .D3(unsigned_4_bit_subtractor_3_d3), .D2(unsigned_4_bit_subtractor_3_d2),
    .D1(unsigned_4_bit_subtractor_3_d1), .D0(unsigned_4_bit_subtractor_3_d0));
  _8_bit_MUX u_8_bit_mux_3 (
    .A0(A1), .A1(n8_bit_mux_2_out_10), .A2(n8_bit_mux_2_out_11), .A3(n8_bit_mux_2_out_12),
    .B0(unsigned_4_bit_subtractor_3_d0), .B1(unsigned_4_bit_subtractor_3_d1),
    .B2(unsigned_4_bit_subtractor_3_d2), .B3(unsigned_4_bit_subtractor_3_d3), .selector(D1),
    .out_10(n8_bit_mux_3_out_10), .out_11(n8_bit_mux_3_out_11), .out_12(n8_bit_mux_3_out_12),
    .out_13(n8_bit_mux_3_out_13));
  _4_bit_Comparaor u_4_bit_comparaor_4 (
    .A0(A0), .A1(n8_bit_mux_3_out_10), .A2(n8_bit_mux_3_out_11), .A3(n8_bit_mux_3_out_12), .B0(B0), .B1(B1),
    .B2(B2), .B3(B3), .out_9(D0), .S(n4_bit_comparaor_4_s));
  Unsigned_4_bit_Subtractor unsigned_4_bit_subtractor_4 (
    .A3(n8_bit_mux_3_out_12), .A2(n8_bit_mux_3_out_11), .A1(n8_bit_mux_3_out_10), .A0(A0), .B3(B3), .B2(B2),
    .B1(B1), .B0(B0), .BORROW_IN_0(1'b0), .Sign(unsigned_4_bit_subtractor_4_sign),
    .D3(unsigned_4_bit_subtractor_4_d3), .D2(unsigned_4_bit_subtractor_4_d2),
    .D1(unsigned_4_bit_subtractor_4_d1), .D0(unsigned_4_bit_subtractor_4_d0));
  _8_bit_MUX u_8_bit_mux_4 (
    .A0(A0), .A1(n8_bit_mux_3_out_10), .A2(n8_bit_mux_3_out_11), .A3(n8_bit_mux_3_out_12),
    .B0(unsigned_4_bit_subtractor_4_d0), .B1(unsigned_4_bit_subtractor_4_d1),
    .B2(unsigned_4_bit_subtractor_4_d2), .B3(unsigned_4_bit_subtractor_4_d3), .selector(D0), .out_10(R0),
    .out_11(R1), .out_12(R2), .out_13(R3));

  // Notes on the sheet:
  //   SUBT
  //   COMPAR
  //   L OR E
  //   A3
  //   A3
  //   A2
  //   COMP2
  //   L OR E
  //   SUB2
  //   MUX2
  //   COMP3
  //   SUB3
  //   MUX3
  //   COMP4
  //   MUX4
  //   sub4
endmodule
