// Logisim project Signed Full Adder.circ as structural Verilog: 10 circuits, main circuit Signed Full Adder
module Signed_Full_Adder (
  input  A0,
  input  A1,
  input  A2,
  input  A3,
  input  A4,
  input  B0,
  input  B1,
  input  B2,
  input  B3,
  input  B4,
  output Sign,
  output S4,
  output S3,
  output S2,
  output S1,
  output S0
);

  wire and_1_out, full_adder_subtractor_1_out_16, full_adder_subtractor_1_out_17, not_1_out, xor_1_out;

  xor xor_1 (xor_1_out, A4, B4);
  not not_1 (not_1_out, xor_1_out);
  Full_Adder_Subtractor full_adder_subtractor_1 (
    .in_1(xor_1_out), .in_2(A0), .in_3(A1), .in_4(A2), .in_5(A3), .in_6(A4), .in_7(B0), .in_8(B1), .in_9(B2),
    .in_10(B3), .in_11(B4), .out_12(S0), .out_13(S1), .out_14(S2), .out_15(S3),
    .out_16(full_adder_subtractor_1_out_16), .out_17(full_adder_subtractor_1_out_17));
  and and_1 (and_1_out, B4, A4);
  and and_2 (S4, not_1_out, full_adder_subtractor_1_out_16);
  and and_3 (Sign, and_1_out, full_adder_subtractor_1_out_17);

  // Notes on the sheet:
  //   LSB
  //   MSB
  //   LSB
  //   MSB
  //   MSB
  //   LSB
endmodule

// HA
module _1_bit_Half_Adder (
  input  An,
  input  Bn,
  output Sn,
  output Cn
);

  xor xor_1 (Sn, An, Bn);
  and and_1 (Cn, An, Bn);
endmodule

// FA
module _1_bit_Full_Adder (
  input  An,
  input  Bn,
  input  C_in_n,
  output Sn,
  output Cn
);

  wire n1_bit_half_adder_1_cn, n1_bit_half_adder_1_sn, n1_bit_half_adder_2_cn;

  _1_bit_Half_Adder u_1_bit_half_adder_1 (.An(An), .Bn(Bn), .Sn(n1_bit_half_adder_1_sn), .Cn(n1_bit_half_adder_1_cn));
  _1_bit_Half_Adder u_1_bit_half_adder_2 (
    .An(n1_bit_half_adder_1_sn), .Bn(C_in_n), .Sn(Sn), .Cn(n1_bit_half_adder_2_cn));
  or or_1 (Cn, n1_bit_half_adder_2_cn, n1_bit_half_adder_1_cn);
endmodule

module _5_bit_Full_Adder (
  input  in_1,
  input  in_2,
  input  in_3,
  input  in_4,
  input  in_5,
  input  in_6,
  input  in_7,
  input  in_8,
  input  in_9,
  input  in_10,
  output out_11,
  output out_12,
  output out_13,
  output out_14,
  output out_15,
  output out_16
);

  wire n1_bit_full_adder_1_cn, n1_bit_full_adder_2_cn, n1_bit_full_adder_3_cn, n1_bit_full_adder_4_cn;

  _1_bit_Full_Adder u_1_bit_full_adder_1 (
    .An(in_1), .Bn(in_6), .C_in_n(1'b0), .Sn(out_11), .Cn(n1_bit_full_adder_1_cn));
  _1_bit_Full_Adder u_1_bit_full_adder_2 (
    .An(in_2), .Bn(in_7), .C_in_n(n1_bit_full_adder_1_cn), .Sn(out_12), .Cn(n1_bit_full_adder_2_cn));
  _1_bit_Full_Adder u_1_bit_full_adder_3 (
    .An(in_3), .Bn(in_8), .C_in_n(n1_bit_full_adder_2_cn), .Sn(out_13), .Cn(n1_bit_full_adder_3_cn));
  _1_bit_Full_Adder u_1_bit_full_adder_4 (
    .An(in_4), .Bn(in_9), .C_in_n(n1_bit_full_adder_3_cn), .Sn(out_14), .Cn(n1_bit_full_adder_4_cn));
  _1_bit_Full_Adder u_1_bit_full_adder_5 (
    .An(in_5), .Bn(in_10), .C_in_n(n1_bit_full_adder_4_cn), .Sn(out_15), .Cn(out_16));
endmodule

module _2_s_Complement (
  input  in_1,
  input  in_2,
  input  in_3,
  input  in_4,
  input  in_5,
  output out_6,
  output out_7,
  output out_8,
  output out_9,
  output out_10
);

  wire not_1_out, not_2_out, not_3_out, not_4_out, not_5_out;

  not not_1 (not_1_out, in_1);
  not not_2 (not_2_out, in_2);
  not not_3 (not_3_out, in_3);
  not not_4 (not_4_out, in_4);
  not not_5 (not_5_out, in_5);
  _5_bit_Full_Adder u_5_bit_full_adder_1 (
    .in_1(not_1_out), .in_2(not_2_out), .in_3(not_3_out), .in_4(not_4_out), .in_5(not_5_out), .in_6(1'b1),
    .in_7(1'b0), .in_8(1'b0), .in_9(1'b0), .in_10(1'b0), .out_11(out_6), .out_12(out_7), .out_13(out_8),
    .out_14(out_9), .out_15(out_10));  // open: out_16
endmodule

module Full_Adder_Subtractor (
  input  in_1,
  input  in_2,
  input  in_3,
  input  in_4,
  input  in_5,
  input  in_6,
  input  in_7,
  input  in_8,
  input  in_9,
  input  in_10,
  input  in_11,
  output out_12,
  output out_13,
  output out_14,
  output out_15,
  output out_16,
  output out_17
);

  wire n1_bit_full_adder_1_cn, n1_bit_full_adder_2_cn, n1_bit_full_adder_3_cn, n1_bit_full_adder_4_cn,
       xor_1_out, xor_2_out, xor_3_out, xor_4_out, xor_5_out;

  xor xor_1 (xor_1_out, in_7, in_1);
  xor xor_2 (xor_2_out, in_8, in_1);
  xor xor_3 (xor_3_out, in_9, in_1);
  xor xor_4 (xor_4_out, in_10, in_1);
  xor xor_5 (xor_5_out, in_1, in_11);
  _1_bit_Full_Adder u_1_bit_full_adder_1 (
    .An(in_2), .Bn(xor_1_out), .C_in_n(in_1), .Sn(out_12), .Cn(n1_bit_full_adder_1_cn));
  _1_bit_Full_Adder u_1_bit_full_adder_2 (
    .An(in_3), .Bn(xor_2_out), .C_in_n(n1_bit_full_adder_1_cn), .Sn(out_13), .Cn(n1_bit_full_adder_2_cn));
  _1_bit_Full_Adder u_1_bit_full_adder_3 (
    .An(in_4), .Bn(xor_3_out), .C_in_n(n1_bit_full_adder_2_cn), .Sn(out_14), .Cn(n1_bit_full_adder_3_cn));
  _1_bit_Full_Adder u_1_bit_full_adder_4 (
    .An(in_5), .Bn(xor_4_out), .C_in_n(n1_bit_full_adder_3_cn), .Sn(out_15), .Cn(n1_bit_full_adder_4_cn));
  _1_bit_Full_Adder u_1_bit_full_adder_5 (
    .An(in_6), .Bn(xor_5_out), .C_in_n(n1_bit_full_adder_4_cn), .Sn(out_16), .Cn(out_17));
endmodule

module _1_bit_Binary_to_BCD (
  input  A,
  input  B,
  input  C,
  input  D,
  output out_5,
  output out_6,
  output out_7,
  output out_8
);

  wire and_1_out, and_2_out, and_3_out, and_4_out, and_5_out, and_6_out, and_7_out, and_8_out, and_9_out,
       and_10_out, not_1_out, not_2_out, not_3_out, not_4_out, not_5_out, not_6_out, not_7_out, not_8_out,
       not_9_out;

  and and_1 (and_1_out, B, C);
  and and_2 (and_2_out, D, B);
  not not_1 (not_1_out, C);
  not not_2 (not_2_out, D);
  not not_3 (not_3_out, C);
  not not_4 (not_4_out, D);
  not not_5 (not_5_out, B);
  and and_3 (and_3_out, B, not_1_out, not_2_out);
  and and_4 (and_4_out, C, D);
  and and_5 (and_5_out, not_3_out, not_4_out, A);
  not not_6 (not_6_out, A);
  not not_7 (not_7_out, A);
  not not_8 (not_8_out, C);
  not not_9 (not_9_out, D);
  and and_6 (and_6_out, D, A);
  and and_7 (and_7_out, not_6_out, not_5_out, C);
  and and_8 (and_8_out, not_5_out, not_7_out, D);
  and and_9 (and_9_out, A, not_8_out, not_9_out);
  and and_10 (and_10_out, not_9_out, B, C);
  or or_1 (out_5, A, and_1_out, and_2_out);
  or or_2 (out_6, and_6_out, and_3_out);
  or or_3 (out_7, and_4_out, and_5_out, and_7_out);
  or or_4 (out_8, and_8_out, and_9_out, and_10_out);

  // Notes on the sheet:
  //   A'B'C
  //   A'B'D
  //   AC'D'
  //   BCD'
endmodule

module _8_bit_Binary_to_BCD (
  input  B7,
  input  B6,
  input  B5,
  input  B4,
  input  B3,
  input  B2,
  input  B1,
  input  B0,
  output P9,
  output P8,
  output P7,
  output P6,
  output P5,
  output P4,
  output P3,
  output P2,
  output P1,
  output P0
);

  wire n1_bit_binary_to_bcd_1_out_5, n1_bit_binary_to_bcd_1_out_6, n1_bit_binary_to_bcd_1_out_7,
       n1_bit_binary_to_bcd_1_out_8, n1_bit_binary_to_bcd_2_out_5, n1_bit_binary_to_bcd_2_out_6,
       n1_bit_binary_to_bcd_2_out_7, n1_bit_binary_to_bcd_2_out_8, n1_bit_binary_to_bcd_3_out_5,
       n1_bit_binary_to_bcd_3_out_6, n1_bit_binary_to_bcd_3_out_7, n1_bit_binary_to_bcd_3_out_8,
       n1_bit_binary_to_bcd_4_out_6, n1_bit_binary_to_bcd_4_out_7, n1_bit_binary_to_bcd_4_out_8,
       n1_bit_binary_to_bcd_5_out_5, n1_bit_binary_to_bcd_5_out_6, n1_bit_binary_to_bcd_5_out_7,
       n1_bit_binary_to_bcd_5_out_8;

  _1_bit_Binary_to_BCD u_1_bit_binary_to_bcd_1 (
    .A(1'b0), .B(B7), .C(B6), .D(B5), .out_5(n1_bit_binary_to_bcd_1_out_5),
    .out_6(n1_bit_binary_to_bcd_1_out_6), .out_7(n1_bit_binary_to_bcd_1_out_7),
    .out_8(n1_bit_binary_to_bcd_1_out_8));
  _1_bit_Binary_to_BCD u_1_bit_binary_to_bcd_2 (
    .A(n1_bit_binary_to_bcd_1_out_6), .B(n1_bit_binary_to_bcd_1_out_7), .C(n1_bit_binary_to_bcd_1_out_8),
    .D(B4), .out_5(n1_bit_binary_to_bcd_2_out_5), .out_6(n1_bit_binary_to_bcd_2_out_6),
    .out_7(n1_bit_binary_to_bcd_2_out_7), .out_8(n1_bit_binary_to_bcd_2_out_8));
  _1_bit_Binary_to_BCD u_1_bit_binary_to_bcd_3 (
    .A(n1_bit_binary_to_bcd_2_out_6), .B(n1_bit_binary_to_bcd_2_out_7), .C(n1_bit_binary_to_bcd_2_out_8),
    .D(B3), .out_5(n1_bit_binary_to_bcd_3_out_5), .out_6(n1_bit_binary_to_bcd_3_out_6),
    .out_7(n1_bit_binary_to_bcd_3_out_7), .out_8(n1_bit_binary_to_bcd_3_out_8));
  _1_bit_Binary_to_BCD u_1_bit_binary_to_bcd_4 (
    .A(1'b0), .B(n1_bit_binary_to_bcd_1_out_5), .C(n1_bit_binary_to_bcd_2_out_5),
    .D(n1_bit_binary_to_bcd_3_out_5), .out_5(P9), .out_6(n1_bit_binary_to_bcd_4_out_6),
    .out_7(n1_bit_binary_to_bcd_4_out_7), .out_8(n1_bit_binary_to_bcd_4_out_8));
  _1_bit_Binary_to_BCD u_1_bit_binary_to_bcd_5 (
    .A(n1_bit_binary_to_bcd_3_out_6), .B(n1_bit_binary_to_bcd_3_out_7), .C(n1_bit_binary_to_bcd_3_out_8),
    .D(B2), .out_5(n1_bit_binary_to_bcd_5_out_5), .out_6(n1_bit_binary_to_bcd_5_out_6),
    .out_7(n1_bit_binary_to_bcd_5_out_7), .out_8(n1_bit_binary_to_bcd_5_out_8));
  _1_bit_Binary_to_BCD u_1_bit_binary_to_bcd_6 (
    .A(n1_bit_binary_to_bcd_4_out_6), .B(n1_bit_binary_to_bcd_4_out_7), .C(n1_bit_binary_to_bcd_4_out_8),
    .D(n1_bit_binary_to_bcd_5_out_5), .out_5(P8), .out_6(P7), .out_7(P6), .out_8(P5));
  _1_bit_Binary_to_BCD u_1_bit_binary_to_bcd_7 (
    .A(n1_bit_binary_to_bcd_5_out_6), .B(n1_bit_binary_to_bcd_5_out_7), .C(n1_bit_binary_to_bcd_5_out_8),
    .D(B1), .out_5(P4), .out_6(P3), .out_7(P2), .out_8(P1));

  assign P0 = B0;
endmodule

module BCD_to_7_Segments (
  input  A,
  input  B,
  input  C,
  input  D,
  output a_2,
  output b_2,
  output c_2,
  output d_2,
  output e,
  output f,
  output g
);

  wire B_prime_C_out, B_prime_D_prime_out, BC_prime_D_out, BC_prime_out, BD_out, BD_prime_out,
       C_prime_D_prime_out, CD_out, CD_prime_out, not_1_out, not_2_out, not_3_out, not_4_out;

  not not_1 (not_1_out, A);
  not not_2 (not_2_out, B);
  not not_3 (not_3_out, C);
  not not_4 (not_4_out, D);
  and BD (BD_out, B, D);
  and B_prime_D_prime (B_prime_D_prime_out, not_2_out, not_4_out);
  and CD (CD_out, C, D);
  and C_prime_D_prime (C_prime_D_prime_out, not_3_out, not_4_out);
  and CD_prime (CD_prime_out, C, not_4_out);
  and B_prime_C (B_prime_C_out, not_2_out, C);
  and BC_prime_D (BC_prime_D_out, D, BC_prime_out);
  and BC_prime (BC_prime_out, B, not_3_out);
  and BD_prime (BD_prime_out, B, not_4_out);
  or u_a (a_2, BD_out, B_prime_D_prime_out, C, A);
  or u_b (b_2, CD_out, C_prime_D_prime_out, not_2_out);
  or u_c (c_2, D, not_3_out, B);
  or u_d (d_2, B_prime_D_prime_out, A, CD_prime_out, B_prime_C_out, BC_prime_D_out);
  or u_e (e, B_prime_D_prime_out, CD_prime_out);
  or u_f (f, C_prime_D_prime_out, BC_prime_out, BD_prime_out, A);
  or u_g (g, CD_prime_out, BC_prime_out, B_prime_C_out, A);
endmodule

module Binary_to_7_Segments (
  input  A0,
  input  A1,
  input  A2,
  input  A3,
  input  A4,
  input  B0,
  input  B1,
  input  B2,
  input  B3,
  input  B4,
  output Sign
);

  wire bcd_to_7_segments_1_a_2, bcd_to_7_segments_1_b_2, bcd_to_7_segments_1_c_2, bcd_to_7_segments_1_d_2,
       bcd_to_7_segments_1_e, bcd_to_7_segments_1_f, bcd_to_7_segments_1_g, bcd_to_7_segments_2_a_2,
       bcd_to_7_segments_2_b_2, bcd_to_7_segments_2_c_2, bcd_to_7_segments_2_d_2, bcd_to_7_segments_2_e,
       bcd_to_7_segments_2_f, bcd_to_7_segments_2_g, bcd_to_7_segments_3_a_2, bcd_to_7_segments_3_b_2,
       bcd_to_7_segments_3_c_2, bcd_to_7_segments_3_d_2, bcd_to_7_segments_3_e, bcd_to_7_segments_3_f,
       bcd_to_7_segments_3_g, n8_bit_binary_to_bcd_1_p0, n8_bit_binary_to_bcd_1_p1,
       n8_bit_binary_to_bcd_1_p2, n8_bit_binary_to_bcd_1_p3, n8_bit_binary_to_bcd_1_p4,
       n8_bit_binary_to_bcd_1_p5, n8_bit_binary_to_bcd_1_p6, n8_bit_binary_to_bcd_1_p7,
       n8_bit_binary_to_bcd_1_p8, n8_bit_binary_to_bcd_1_p9, signed_full_adder_1_s1, signed_full_adder_1_s2,
       signed_full_adder_1_s3, signed_full_adder_1_s4, signed_full_adder_1_sign;

  Signed_Full_Adder signed_full_adder_1 (
    .A0(A0), .A1(A1), .A2(A2), .A3(A3), .A4(A4), .B0(B0), .B1(B1), .B2(B2), .B3(B3), .B4(B4),
    .Sign(signed_full_adder_1_sign), .S4(signed_full_adder_1_s4), .S3(signed_full_adder_1_s3),
    .S2(signed_full_adder_1_s2), .S1(signed_full_adder_1_s1), .S0(Sign));
  _8_bit_Binary_to_BCD u_8_bit_binary_to_bcd_1 (
    .B7(1'b0), .B6(1'b0), .B5(1'b0), .B4(signed_full_adder_1_sign), .B3(signed_full_adder_1_s4),
    .B2(signed_full_adder_1_s3), .B1(signed_full_adder_1_s2), .B0(signed_full_adder_1_s1),
    .P9(n8_bit_binary_to_bcd_1_p9), .P8(n8_bit_binary_to_bcd_1_p8), .P7(n8_bit_binary_to_bcd_1_p7),
    .P6(n8_bit_binary_to_bcd_1_p6), .P5(n8_bit_binary_to_bcd_1_p5), .P4(n8_bit_binary_to_bcd_1_p4),
    .P3(n8_bit_binary_to_bcd_1_p3), .P2(n8_bit_binary_to_bcd_1_p2), .P1(n8_bit_binary_to_bcd_1_p1),
    .P0(n8_bit_binary_to_bcd_1_p0));
  BCD_to_7_Segments bcd_to_7_segments_1 (
    .A(1'b0), .B(1'b0), .C(n8_bit_binary_to_bcd_1_p9), .D(n8_bit_binary_to_bcd_1_p8),
    .a_2(bcd_to_7_segments_1_a_2), .b_2(bcd_to_7_segments_1_b_2), .c_2(bcd_to_7_segments_1_c_2),
    .d_2(bcd_to_7_segments_1_d_2), .e(bcd_to_7_segments_1_e), .f(bcd_to_7_segments_1_f),
    .g(bcd_to_7_segments_1_g));
  BCD_to_7_Segments bcd_to_7_segments_2 (
    .A(n8_bit_binary_to_bcd_1_p7), .B(n8_bit_binary_to_bcd_1_p6), .C(n8_bit_binary_to_bcd_1_p5),
    .D(n8_bit_binary_to_bcd_1_p4), .a_2(bcd_to_7_segments_2_a_2), .b_2(bcd_to_7_segments_2_b_2),
    .c_2(bcd_to_7_segments_2_c_2), .d_2(bcd_to_7_segments_2_d_2), .e(bcd_to_7_segments_2_e),
    .f(bcd_to_7_segments_2_f), .g(bcd_to_7_segments_2_g));
  BCD_to_7_Segments bcd_to_7_segments_3 (
    .A(n8_bit_binary_to_bcd_1_p3), .B(n8_bit_binary_to_bcd_1_p2), .C(n8_bit_binary_to_bcd_1_p1),
    .D(n8_bit_binary_to_bcd_1_p0), .a_2(bcd_to_7_segments_3_a_2), .b_2(bcd_to_7_segments_3_b_2),
    .c_2(bcd_to_7_segments_3_c_2), .d_2(bcd_to_7_segments_3_d_2), .e(bcd_to_7_segments_3_e),
    .f(bcd_to_7_segments_3_f), .g(bcd_to_7_segments_3_g));
  _7_Segment_Display u_7_segment_display_1 (
    .g(bcd_to_7_segments_1_g), .f(bcd_to_7_segments_1_f), .a(bcd_to_7_segments_1_a_2),
    .b(bcd_to_7_segments_1_b_2), .e(bcd_to_7_segments_1_e), .d(bcd_to_7_segments_1_d_2),
    .c(bcd_to_7_segments_1_c_2));  // open: dp
  _7_Segment_Display u_7_segment_display_2 (
    .g(bcd_to_7_segments_2_g), .f(bcd_to_7_segments_2_f), .a(bcd_to_7_segments_2_a_2),
    .b(bcd_to_7_segments_2_b_2), .e(bcd_to_7_segments_2_e), .d(bcd_to_7_segments_2_d_2),
    .c(bcd_to_7_segments_2_c_2));  // open: dp
  _7_Segment_Display u_7_segment_display_3 (
    .g(bcd_to_7_segments_3_g), .f(bcd_to_7_segments_3_f), .a(bcd_to_7_segments_3_a_2),
    .b(bcd_to_7_segments_3_b_2), .e(bcd_to_7_segments_3_e), .d(bcd_to_7_segments_3_d_2),
    .c(bcd_to_7_segments_3_c_2));  // open: dp
endmodule
