// Logisim project sign management.circ as structural Verilog: 6 circuits, main circuit main
module main (
  input  signal_1,
  input  signal_2,
  input  A_sign,
  input  B_sign
);

  wire sign_manager_1_out_1, sign_manager_1_out_2;

  sign_manager sign_manager_1 (
    .signal_1(signal_1), .signal_2(signal_2), .A_sign(A_sign), .B_sign(B_sign), .out_1(sign_manager_1_out_1),
    .out_2(sign_manager_1_out_2));  // open: sign, exchange
  op_selector op_selector_1 (.out_1(sign_manager_1_out_1), .out_2(sign_manager_1_out_2));  // open: Add, sub, multi, div
endmodule

module out_2 (
  input  signal_1,
  input  signal_2,
  input  A_sign,
  input  B_sign,
  output out_2
);

  wire AB_out, and_1_out, and_2_out, not_1_out, not_2_out, not_3_out, xor_1_out;

  not not_1 (not_1_out, signal_1);
  not not_2 (not_2_out, signal_2);
  xor xor_1 (xor_1_out, A_sign, B_sign);
  and AB (AB_out, signal_1, signal_2);
  not not_3 (not_3_out, xor_1_out);
  and and_1 (and_1_out, not_1_out, not_2_out, xor_1_out);
  and and_2 (and_2_out, not_3_out, signal_2);
  or or_1 (out_2, AB_out, and_1_out, and_2_out);
endmodule

module sign (
  input  signal_1,
  input  signal_2,
  input  A_sign,
  input  B_sign,
  output sign
);

  wire and_1_out, and_2_out, and_3_out, and_4_out, not_1_out, not_2_out, not_3_out, not_4_out, not_5_out;

  not not_1 (not_1_out, signal_1);
  not not_2 (not_2_out, signal_2);
  not not_3 (not_3_out, B_sign);
  not not_4 (not_4_out, A_sign);
  not not_5 (not_5_out, B_sign);
  and and_1 (and_1_out, not_1_out, not_2_out, A_sign, B_sign);
  and and_2 (and_2_out, signal_2, A_sign, not_3_out);
  and and_3 (and_3_out, signal_1, not_4_out, B_sign);
  and and_4 (and_4_out, signal_1, A_sign, not_5_out);
  or or_1 (sign, and_1_out, and_2_out, and_3_out, and_4_out);
endmodule

module exchange (
  input  signal_1,
  input  signal_2,
  input  A_sign,
  input  B_sign,
  output Exchange
);

  wire and_1_out, and_2_out, not_1_out, not_2_out, not_3_out, not_4_out;

  not not_1 (not_1_out, signal_1);
  not not_2 (not_2_out, signal_2);
  not not_3 (not_3_out, B_sign);
  not not_4 (not_4_out, signal_1);
  and and_1 (and_1_out, not_1_out, not_2_out, A_sign, not_3_out);
  and and_2 (and_2_out, not_4_out, signal_2, A_sign, B_sign);
  or or_1 (Exchange, and_1_out, and_2_out);
endmodule

module sign_manager (
  input  signal_1,
  input  signal_2,
  input  A_sign,
  input  B_sign,
  output out_1,
  output out_2,
  output sign,
  output exchange
);

  out_2 out_2_1 (.signal_1(signal_1), .signal_2(signal_2), .A_sign(A_sign), .B_sign(B_sign), .out_2(out_2));
  sign sign_1 (.signal_1(signal_1), .signal_2(signal_2), .A_sign(A_sign), .B_sign(B_sign), .sign(sign));
  exchange exchange_1 (.signal_1(signal_1), .signal_2(signal_2), .A_sign(A_sign), .B_sign(B_sign), .Exchange(exchange));

  assign out_1 = signal_1;
endmodule

module op_selector (
  input  out_1,
  input  out_2,
  output Add,
  output sub,
  output multi,
  output div
);

  wire not_1_out, not_2_out;

  not not_1 (not_1_out, out_1);
  not not_2 (not_2_out, out_2);
  and and_1 (Add, not_1_out, not_2_out);
  and and_2 (sub, not_1_out, out_2);
  and and_3 (multi, out_1, not_2_out);
  and and_4 (div, out_1, out_2);
endmodule
